// Logisim project ALU.circ as structural Verilog: 10 circuits, main circuit ALU
module Board (
  input  [7:0] in_1,
  input  [7:0] in_2,
  input  in_3,
  input  in_4,
  input  in_5,
  input  in_6
);

  wire alu_1_neg, alu_1_overflow, userbcdto7seg_1_a, userbcdto7seg_1_b, userbcdto7seg_1_c, userbcdto7seg_1_d,
       userbcdto7seg_1_e, userbcdto7seg_1_f, userbcdto7seg_1_g, userbcdto7seg_2_a, userbcdto7seg_2_b,
       userbcdto7seg_2_c, userbcdto7seg_2_d, userbcdto7seg_2_e, userbcdto7seg_2_f, userbcdto7seg_2_g,
       userbcdto7seg_3_a, userbcdto7seg_3_b, userbcdto7seg_3_c, userbcdto7seg_3_d, userbcdto7seg_3_e,
       userbcdto7seg_3_f, userbcdto7seg_3_g;
  wire [3:0] binary_to_bcd_converter_1_p2, binary_to_bcd_converter_1_p3, binary_to_bcd_converter_1_p4;
  wire [7:0] alu_1_lsb;

  LED led_1 (.in(alu_1_overflow));
  LED led_2 (.in(alu_1_neg));
  UserBCDto7Seg userbcdto7seg_1 (
    .D3(binary_to_bcd_converter_1_p2[3]), .D2(binary_to_bcd_converter_1_p2[2]),
    .D1(binary_to_bcd_converter_1_p2[1]), .Do(binary_to_bcd_converter_1_p2[0]), .a(userbcdto7seg_1_a),
    .g(userbcdto7seg_1_g), .f(userbcdto7seg_1_f), .e(userbcdto7seg_1_e), .d(userbcdto7seg_1_d),
    .c(userbcdto7seg_1_c), .b(userbcdto7seg_1_b));
  ALU alu_1 (
    .A7(in_1[7]), .A6(in_1[6]), .A5(in_1[5]), .A4(in_1[4]), .A3(in_1[3]), .A2(in_1[2]), .A1(in_1[1]),
    .Ao(in_1[0]), .B7(in_2[7]), .B6(in_2[6]), .B5(in_2[5]), .B4(in_2[4]), .B3(in_2[3]), .B2(in_2[2]),
    .B1(in_2[1]), .Bo(in_2[0]), .ADD(in_3), .SUB(in_4), .MUL(in_5), .DIV(in_6), .neg(alu_1_neg),
    .MSB(alu_1_lsb[7]), .out_24(alu_1_lsb[6]), .out_25(alu_1_lsb[5]), .out_26(alu_1_lsb[4]),
    .out_27(alu_1_lsb[3]), .out_28(alu_1_lsb[2]), .out_29(alu_1_lsb[1]), .LSB(alu_1_lsb[0]),
    .OVERFLOW(alu_1_overflow));
  _7_Segment_Display u_7_segment_display_1 (
    .g(userbcdto7seg_1_g), .f(userbcdto7seg_1_f), .a(userbcdto7seg_1_a), .b(userbcdto7seg_1_b),
    .e(userbcdto7seg_1_e), .d(userbcdto7seg_1_d), .c(userbcdto7seg_1_c));  // open: dp
  UserBCDto7Seg userbcdto7seg_2 (
    .D3(binary_to_bcd_converter_1_p3[3]), .D2(binary_to_bcd_converter_1_p3[2]),
    .D1(binary_to_bcd_converter_1_p3[1]), .Do(binary_to_bcd_converter_1_p3[0]), .a(userbcdto7seg_2_a),
    .g(userbcdto7seg_2_g), .f(userbcdto7seg_2_f), .e(userbcdto7seg_2_e), .d(userbcdto7seg_2_d),
    .c(userbcdto7seg_2_c), .b(userbcdto7seg_2_b));
  // Binary_to_BCD_converter #(.binvalue(8)) binary_to_bcd_converter_1: pin names not known; wires that end beside it: alu_1_lsb, binary_to_bcd_converter_1_p2, binary_to_bcd_converter_1_p3, binary_to_bcd_converter_1_p4
  _7_Segment_Display u_7_segment_display_2 (
    .g(userbcdto7seg_2_g), .f(userbcdto7seg_2_f), .a(userbcdto7seg_2_a), .b(userbcdto7seg_2_b),
    .e(userbcdto7seg_2_e), .d(userbcdto7seg_2_d), .c(userbcdto7seg_2_c));  // open: dp
  UserBCDto7Seg userbcdto7seg_3 (
    .D3(binary_to_bcd_converter_1_p4[3]), .D2(binary_to_bcd_converter_1_p4[2]),
    .D1(binary_to_bcd_converter_1_p4[1]), .Do(binary_to_bcd_converter_1_p4[0]), .a(userbcdto7seg_3_a),
    .g(userbcdto7seg_3_g), .f(userbcdto7seg_3_f), .e(userbcdto7seg_3_e), .d(userbcdto7seg_3_d),
    .c(userbcdto7seg_3_c), .b(userbcdto7seg_3_b));
  _7_Segment_Display u_7_segment_display_3 (
    .g(userbcdto7seg_3_g), .f(userbcdto7seg_3_f), .a(userbcdto7seg_3_a), .b(userbcdto7seg_3_b),
    .e(userbcdto7seg_3_e), .d(userbcdto7seg_3_d), .c(userbcdto7seg_3_c));  // open: dp
endmodule

module ALU (
  input  ADD,
  input  SUB,
  input  MUL,
  input  DIV,
  input  A7,
  input  A6,
  input  A5,
  input  A4,
  input  A3,
  input  A2,
  input  A1,
  input  Ao,
  input  B7,
  input  B6,
  input  B5,
  input  B4,
  input  B3,
  input  B2,
  input  B1,
  input  Bo,
  output OVERFLOW,
  output neg,
  output MSB,
  output out_24,
  output out_25,
  output out_26,
  output out_27,
  output out_28,
  output out_29,
  output LSB
);

  wire or_1_out, useraddandsub_1_lsb, useraddandsub_1_msb, useraddandsub_1_neglect, useraddandsub_1_out_22,
       useraddandsub_1_out_23, useraddandsub_1_out_24, useraddandsub_1_out_25, useraddandsub_1_out_26,
       useraddandsub_1_out_27, userdivider_1_lsb, userdivider_1_msb, userdivider_1_out_19,
       userdivider_1_out_20, userdivider_1_out_21, userdivider_1_out_22, userdivider_1_out_23,
       userdivider_1_out_24, usermultiplier_1_lsb, usermultiplier_1_msb, usermultiplier_1_out_19,
       usermultiplier_1_out_20, usermultiplier_1_out_21, usermultiplier_1_out_22, usermultiplier_1_out_23,
       usermultiplier_1_out_24, usermultiplier_1_out_25, usermultiplier_1_out_26, usermultiplier_1_out_27,
       usermultiplier_1_out_28, usermultiplier_1_out_29, usermultiplier_1_out_30, usermultiplier_1_out_31,
       usermultiplier_1_out_32;

  or or_1 (or_1_out, ADD, SUB);
  UserAddAndSub useraddandsub_1 (
    .A3(A3), .A4(A4), .A5(A5), .Ao(Ao), .A6(A6), .A7(A7), .A1(A1), .A2(A2), .SubtractionBit(SUB), .Bo(Bo),
    .B1(B1), .B2(B2), .B3(B3), .B4(B4), .B5(B5), .B6(B6), .B7(B7), .Enable(or_1_out),
    .neglect(useraddandsub_1_neglect), .NegativeSign(neg), .MSB(useraddandsub_1_msb),
    .out_22(useraddandsub_1_out_22), .out_23(useraddandsub_1_out_23), .out_24(useraddandsub_1_out_24),
    .out_25(useraddandsub_1_out_25), .out_26(useraddandsub_1_out_26), .out_27(useraddandsub_1_out_27),
    .LSB(useraddandsub_1_lsb));
  UserDivider userdivider_1 (
    .E(DIV), .A7(A7), .A6(A6), .A5(A5), .A4(A4), .A3(A3), .A2(A2), .A1(A1), .Ao(Ao), .B7(B7), .B6(B6),
    .B5(B5), .B4(B4), .B3(B3), .B2(B2), .B1(B1), .Bo(Bo), .LSB(userdivider_1_lsb),
    .out_19(userdivider_1_out_19), .out_20(userdivider_1_out_20), .out_21(userdivider_1_out_21),
    .out_22(userdivider_1_out_22), .out_23(userdivider_1_out_23), .out_24(userdivider_1_out_24),
    .MSB(userdivider_1_msb));
  or or_2 (OVERFLOW, useraddandsub_1_neglect, usermultiplier_1_msb, usermultiplier_1_out_19, usermultiplier_1_out_20, usermultiplier_1_out_21, usermultiplier_1_out_22, usermultiplier_1_out_23, usermultiplier_1_out_24, usermultiplier_1_out_25);
  UserMultiplier usermultiplier_1 (
    .Enable(MUL), .A7(A7), .A6(A6), .A5(A5), .A4(A4), .A3(A3), .A2(A2), .A1(A1), .Ao(Ao), .B7(B7), .B6(B6),
    .B5(B5), .B4(B4), .B3(B3), .B2(B2), .B1(B1), .Bo(Bo), .MSB(usermultiplier_1_msb),
    .out_19(usermultiplier_1_out_19), .out_20(usermultiplier_1_out_20), .out_21(usermultiplier_1_out_21),
    .out_22(usermultiplier_1_out_22), .out_23(usermultiplier_1_out_23), .out_24(usermultiplier_1_out_24),
    .out_25(usermultiplier_1_out_25), .out_26(usermultiplier_1_out_26), .out_27(usermultiplier_1_out_27),
    .out_28(usermultiplier_1_out_28), .out_29(usermultiplier_1_out_29), .out_30(usermultiplier_1_out_30),
    .out_31(usermultiplier_1_out_31), .out_32(usermultiplier_1_out_32), .LSB(usermultiplier_1_lsb));
  or or_3 (MSB, useraddandsub_1_msb, usermultiplier_1_out_26, userdivider_1_msb);
  or or_4 (out_24, useraddandsub_1_out_22, usermultiplier_1_out_27, userdivider_1_out_24);
  or or_5 (out_25, useraddandsub_1_out_23, usermultiplier_1_out_28, userdivider_1_out_23);
  or or_6 (out_26, useraddandsub_1_out_24, usermultiplier_1_out_29, userdivider_1_out_22);
  or or_7 (out_27, useraddandsub_1_out_25, usermultiplier_1_out_30, userdivider_1_out_21);
  or or_8 (out_28, useraddandsub_1_out_26, usermultiplier_1_out_31, userdivider_1_out_20);
  or or_9 (out_29, useraddandsub_1_out_27, usermultiplier_1_out_32, userdivider_1_out_19);
  or or_10 (LSB, useraddandsub_1_lsb, usermultiplier_1_lsb, userdivider_1_lsb);
endmodule

module UserHalfAdder (
  input  A,
  input  B,
  output S,
  output C
);

  xor xor_1 (S, A, B);
  and and_1 (C, A, B);
endmodule

module UserFullAdder (
  input  Ci,
  input  A,
  input  B,
  output S,
  output Co
);

  wire and_1_out, and_2_out, xor_1_out;

  xor xor_1 (xor_1_out, A, B);
  and and_1 (and_1_out, A, B);
  xor xor_2 (S, Ci, xor_1_out);
  and and_2 (and_2_out, Ci, xor_1_out);
  or or_1 (Co, and_1_out, and_2_out);
endmodule

module UserAddAndSub (
  input  Ao,
  input  Enable,
  input  A1,
  input  A2,
  input  A3,
  input  A4,
  input  A5,
  input  A6,
  input  A7,
  input  SubtractionBit,
  input  Bo,
  input  B1,
  input  B2,
  input  B3,
  input  B4,
  input  B5,
  input  B6,
  input  B7,
  output neglect,
  output NegativeSign,
  output MSB,
  output out_22,
  output out_23,
  output out_24,
  output out_25,
  output out_26,
  output out_27,
  output LSB
);

  wire and_1_out, and_2_out, and_3_out, and_4_out, and_5_out, and_6_out, and_7_out, and_8_out, and_9_out,
       and_10_out, and_11_out, and_12_out, and_13_out, and_14_out, and_15_out, and_16_out,
       userfulladder_1_co, userfulladder_2_co, userfulladder_3_co, userfulladder_4_co, userfulladder_5_co,
       userfulladder_6_co, userfulladder_7_co, xor_1_out, xor_2_out, xor_3_out, xor_4_out, xor_5_out,
       xor_6_out, xor_7_out, xor_8_out;
  wire [7:0] user2scomp_1_out_2, userfulladder_1_s;

  and and_1 (and_1_out, Enable, Bo);
  and and_2 (and_2_out, Enable, B1);
  and and_3 (and_3_out, Enable, B2);
  and and_4 (and_4_out, Enable, B3);
  and and_5 (and_5_out, Enable, B4);
  and and_6 (and_6_out, Enable, B5);
  and and_7 (and_7_out, Enable, B6);
  and and_8 (and_8_out, Enable, B7);
  and and_9 (and_9_out, Enable, Ao);
  and and_10 (and_10_out, Enable, A1);
  and and_11 (and_11_out, Enable, A2);
  and and_12 (and_12_out, Enable, A3);
  and and_13 (and_13_out, Enable, A4);
  and and_14 (and_14_out, Enable, A5);
  and and_15 (and_15_out, Enable, A6);
  and and_16 (and_16_out, Enable, A7);
  xor xor_1 (xor_1_out, SubtractionBit, and_1_out);
  xor xor_2 (xor_2_out, SubtractionBit, and_2_out);
  xor xor_3 (xor_3_out, SubtractionBit, and_3_out);
  xor xor_4 (xor_4_out, SubtractionBit, and_4_out);
  xor xor_5 (xor_5_out, SubtractionBit, and_5_out);
  xor xor_6 (xor_6_out, SubtractionBit, and_6_out);
  xor xor_7 (xor_7_out, SubtractionBit, and_7_out);
  xor xor_8 (xor_8_out, SubtractionBit, and_8_out);
  UserFullAdder userfulladder_1 (
    .A(and_9_out), .B(xor_1_out), .Ci(SubtractionBit), .S(userfulladder_1_s[0]), .Co(userfulladder_1_co));
  and and_17 (NegativeSign, SubtractionBit, userfulladder_1_s[7]);
  UserFullAdder userfulladder_2 (
    .A(and_10_out), .B(xor_2_out), .Ci(userfulladder_1_co), .S(userfulladder_1_s[1]), .Co(userfulladder_2_co));
  UserFullAdder userfulladder_3 (
    .A(and_11_out), .B(xor_3_out), .Ci(userfulladder_2_co), .S(userfulladder_1_s[2]), .Co(userfulladder_3_co));
  Multiplexer #(.width(8)) multiplexer_1 (
    .in0(userfulladder_1_s), .in1(user2scomp_1_out_2),
    .out({MSB, out_22, out_23, out_24, out_25, out_26, out_27, LSB}), .sel(NegativeSign));
  UserFullAdder userfulladder_4 (
    .A(and_12_out), .B(xor_4_out), .Ci(userfulladder_3_co), .S(userfulladder_1_s[3]), .Co(userfulladder_4_co));
  User2sComp user2scomp_1 (.in_1(userfulladder_1_s), .out_2(user2scomp_1_out_2));
  UserFullAdder userfulladder_5 (
    .A(and_13_out), .B(xor_5_out), .Ci(userfulladder_4_co), .S(userfulladder_1_s[4]), .Co(userfulladder_5_co));
  UserFullAdder userfulladder_6 (
    .A(and_14_out), .B(xor_6_out), .Ci(userfulladder_5_co), .S(userfulladder_1_s[5]), .Co(userfulladder_6_co));
  UserFullAdder userfulladder_7 (
    .A(and_15_out), .B(xor_7_out), .Ci(userfulladder_6_co), .S(userfulladder_1_s[6]), .Co(userfulladder_7_co));
  UserFullAdder userfulladder_8 (
    .A(and_16_out), .B(xor_8_out), .Ci(userfulladder_7_co), .S(userfulladder_1_s[7]), .Co(neglect));
endmodule

// HA
module UserMultiplier (
  input  A7,
  input  A6,
  input  A5,
  input  A4,
  input  A3,
  input  A2,
  input  A1,
  input  Ao,
  input  Enable,
  input  B7,
  input  B6,
  input  B5,
  input  B4,
  input  B3,
  input  B2,
  input  B1,
  input  Bo,
  output MSB,
  output out_19,
  output out_20,
  output out_21,
  output out_22,
  output out_23,
  output out_24,
  output out_25,
  output out_26,
  output out_27,
  output out_28,
  output out_29,
  output out_30,
  output out_31,
  output out_32,
  output LSB
);

  wire and_1_out, and_2_out, and_3_out, and_4_out, and_5_out, and_6_out, and_7_out, and_8_out, and_9_out,
       and_10_out, and_11_out, and_12_out, and_13_out, and_14_out, and_15_out, and_16_out, and_17_out,
       and_18_out, and_19_out, and_20_out, and_21_out, and_22_out, and_23_out, and_24_out, and_25_out,
       and_26_out, and_27_out, and_28_out, and_29_out, and_30_out, and_31_out, and_32_out, and_33_out,
       and_34_out, and_35_out, and_36_out, and_37_out, and_38_out, and_39_out, and_40_out, and_41_out,
       and_42_out, and_43_out, and_44_out, and_45_out, and_46_out, and_47_out, and_48_out, and_49_out,
       and_50_out, and_51_out, and_52_out, and_53_out, and_54_out, and_55_out, and_56_out, and_57_out,
       and_58_out, and_59_out, and_60_out, and_61_out, and_62_out, and_63_out, and_64_out, and_65_out,
       and_66_out, and_67_out, and_68_out, and_69_out, and_70_out, and_71_out, and_72_out, and_73_out,
       and_75_out, and_76_out, and_77_out, and_78_out, and_79_out, and_80_out, userfulladder_2_co,
       userfulladder_3_co, userfulladder_3_s, userfulladder_4_co, userfulladder_5_co, userfulladder_5_s,
       userfulladder_6_co, userfulladder_6_s, userfulladder_7_co, userfulladder_7_s, userfulladder_8_co,
       userfulladder_9_co, userfulladder_9_s, userfulladder_10_co, userfulladder_10_s, userfulladder_11_co,
       userfulladder_11_s, userfulladder_12_co, userfulladder_13_co, userfulladder_13_s, userfulladder_14_co,
       userfulladder_14_s, userfulladder_15_co, userfulladder_15_s, userfulladder_16_co, userfulladder_17_co,
       userfulladder_17_s, userfulladder_18_co, userfulladder_18_s, userfulladder_19_co, userfulladder_19_s,
       userfulladder_20_co, userfulladder_20_s, userfulladder_21_co, userfulladder_22_co, userfulladder_22_s,
       userfulladder_23_co, userfulladder_23_s, userfulladder_24_co, userfulladder_24_s, userfulladder_25_co,
       userfulladder_25_s, userfulladder_26_co, userfulladder_26_s, userfulladder_27_co, userfulladder_27_s,
       userfulladder_28_co, userfulladder_28_s, userfulladder_29_co, userfulladder_29_s, userfulladder_30_co,
       userfulladder_30_s, userfulladder_31_co, userfulladder_31_s, userfulladder_32_co, userfulladder_32_s,
       userfulladder_33_co, userfulladder_33_s, userfulladder_34_co, userfulladder_34_s, userfulladder_35_co,
       userfulladder_35_s, userfulladder_36_co, userfulladder_36_s, userfulladder_37_co, userfulladder_37_s,
       userfulladder_38_co, userfulladder_38_s, userfulladder_39_co, userfulladder_39_s, userfulladder_40_co,
       userfulladder_40_s, userfulladder_41_co, userfulladder_41_s, userfulladder_42_co, userfulladder_42_s,
       userfulladder_43_co, userfulladder_43_s, userfulladder_44_co, userfulladder_44_s, userfulladder_45_co,
       userfulladder_45_s, userfulladder_46_co, userfulladder_46_s, userfulladder_47_co, userfulladder_47_s,
       userfulladder_48_co, userfulladder_48_s, userhalfadder_1_c, userhalfadder_2_c, userhalfadder_2_s,
       userhalfadder_3_c, userhalfadder_4_c, userhalfadder_5_c, userhalfadder_6_c, userhalfadder_7_c,
       userhalfadder_8_c;

  and and_1 (and_1_out, and_72_out, and_59_out);
  UserFullAdder userfulladder_1 (.A(userfulladder_3_co), .B(and_1_out), .Ci(userfulladder_2_co), .S(out_19), .Co(MSB));
  and and_2 (and_2_out, and_72_out, and_60_out);
  UserFullAdder userfulladder_2 (
    .A(userfulladder_3_s), .B(and_2_out), .Ci(userfulladder_4_co), .S(out_20), .Co(userfulladder_2_co));
  and and_3 (and_3_out, and_73_out, and_59_out);
  UserFullAdder userfulladder_3 (
    .A(userfulladder_6_co), .B(and_3_out), .Ci(userfulladder_5_co), .S(userfulladder_3_s),
    .Co(userfulladder_3_co));
  UserFullAdder userfulladder_4 (
    .A(userfulladder_5_s), .B(and_5_out), .Ci(userfulladder_8_co), .S(out_21), .Co(userfulladder_4_co));
  and and_4 (and_4_out, and_73_out, and_60_out);
  UserFullAdder userfulladder_5 (
    .A(userfulladder_6_s), .B(and_4_out), .Ci(userfulladder_7_co), .S(userfulladder_5_s),
    .Co(userfulladder_5_co));
  and and_5 (and_5_out, and_72_out, and_64_out);
  and and_6 (and_6_out, and_75_out, and_59_out);
  UserFullAdder userfulladder_6 (
    .A(userfulladder_9_co), .B(and_6_out), .Ci(userfulladder_10_co), .S(userfulladder_6_s),
    .Co(userfulladder_6_co));
  and and_7 (and_7_out, and_73_out, and_64_out);
  UserFullAdder userfulladder_7 (
    .A(userfulladder_10_s), .B(and_7_out), .Ci(userfulladder_11_co), .S(userfulladder_7_s),
    .Co(userfulladder_7_co));
  and and_8 (and_8_out, and_72_out, and_65_out);
  UserFullAdder userfulladder_8 (
    .A(userfulladder_7_s), .B(and_8_out), .Ci(userfulladder_12_co), .S(out_22), .Co(userfulladder_8_co));
  and and_9 (and_9_out, and_76_out, and_59_out);
  UserFullAdder userfulladder_9 (
    .A(userfulladder_17_co), .B(and_9_out), .Ci(userfulladder_13_co), .S(userfulladder_9_s),
    .Co(userfulladder_9_co));
  and and_10 (and_10_out, and_75_out, and_60_out);
  UserFullAdder userfulladder_10 (
    .A(userfulladder_9_s), .B(and_10_out), .Ci(userfulladder_14_co), .S(userfulladder_10_s),
    .Co(userfulladder_10_co));
  and and_11 (and_11_out, and_73_out, and_65_out);
  UserFullAdder userfulladder_11 (
    .A(userfulladder_14_s), .B(and_11_out), .Ci(userfulladder_15_co), .S(userfulladder_11_s),
    .Co(userfulladder_11_co));
  and and_12 (and_12_out, and_72_out, and_66_out);
  UserFullAdder userfulladder_12 (
    .A(userfulladder_11_s), .B(and_12_out), .Ci(userfulladder_16_co), .S(out_23), .Co(userfulladder_12_co));
  and and_13 (and_13_out, and_76_out, and_60_out);
  UserFullAdder userfulladder_13 (
    .A(userfulladder_17_s), .B(and_13_out), .Ci(userfulladder_18_co), .S(userfulladder_13_s),
    .Co(userfulladder_13_co));
  and and_14 (and_14_out, and_75_out, and_64_out);
  UserFullAdder userfulladder_14 (
    .A(userfulladder_13_s), .B(and_14_out), .Ci(userfulladder_19_co), .S(userfulladder_14_s),
    .Co(userfulladder_14_co));
  and and_15 (and_15_out, and_73_out, and_66_out);
  UserFullAdder userfulladder_15 (
    .A(userfulladder_19_s), .B(and_15_out), .Ci(userfulladder_20_co), .S(userfulladder_15_s),
    .Co(userfulladder_15_co));
  and and_16 (and_16_out, and_72_out, and_68_out);
  UserFullAdder userfulladder_16 (
    .A(userfulladder_15_s), .B(and_16_out), .Ci(userfulladder_21_co), .S(out_24), .Co(userfulladder_16_co));
  and and_17 (and_17_out, and_77_out, and_59_out);
  UserFullAdder userfulladder_17 (
    .A(userfulladder_22_co), .B(and_17_out), .Ci(userfulladder_23_co), .S(userfulladder_17_s),
    .Co(userfulladder_17_co));
  and and_18 (and_18_out, and_76_out, and_64_out);
  UserFullAdder userfulladder_18 (
    .A(userfulladder_23_s), .B(and_18_out), .Ci(userfulladder_24_co), .S(userfulladder_18_s),
    .Co(userfulladder_18_co));
  and and_19 (and_19_out, and_75_out, and_65_out);
  UserFullAdder userfulladder_19 (
    .A(userfulladder_18_s), .B(and_19_out), .Ci(userfulladder_25_co), .S(userfulladder_19_s),
    .Co(userfulladder_19_co));
  UserFullAdder userfulladder_20 (
    .A(userfulladder_25_s), .B(and_23_out), .Ci(userfulladder_29_co), .S(userfulladder_20_s),
    .Co(userfulladder_20_co));
  and and_20 (and_20_out, and_72_out, and_69_out);
  UserFullAdder userfulladder_21 (
    .A(userfulladder_20_s), .B(and_20_out), .Ci(userhalfadder_1_c), .S(out_25), .Co(userfulladder_21_co));
  UserFullAdder userfulladder_22 (
    .A(userhalfadder_2_c), .B(and_25_out), .Ci(userfulladder_26_co), .S(userfulladder_22_s),
    .Co(userfulladder_22_co));
  and and_21 (and_21_out, and_77_out, and_60_out);
  UserFullAdder userfulladder_23 (
    .A(userfulladder_22_s), .B(and_21_out), .Ci(userfulladder_27_co), .S(userfulladder_23_s),
    .Co(userfulladder_23_co));
  UserFullAdder userfulladder_24 (
    .A(userfulladder_27_s), .B(and_27_out), .Ci(userfulladder_31_co), .S(userfulladder_24_s),
    .Co(userfulladder_24_co));
  and and_22 (and_22_out, and_75_out, and_66_out);
  UserFullAdder userfulladder_25 (
    .A(userfulladder_24_s), .B(and_22_out), .Ci(userfulladder_28_co), .S(userfulladder_25_s),
    .Co(userfulladder_25_co));
  and and_23 (and_23_out, and_73_out, and_68_out);
  and and_24 (and_24_out, and_72_out, and_70_out);
  UserHalfAdder userhalfadder_1 (.A(userfulladder_29_s), .B(and_24_out), .S(out_26), .C(userhalfadder_1_c));
  and and_25 (and_25_out, and_78_out, and_59_out);
  UserFullAdder userfulladder_26 (
    .A(userhalfadder_2_s), .B(and_31_out), .Ci(userfulladder_34_co), .S(userfulladder_26_s),
    .Co(userfulladder_26_co));
  and and_26 (and_26_out, and_77_out, and_64_out);
  UserFullAdder userfulladder_27 (
    .A(userfulladder_26_s), .B(and_26_out), .Ci(userfulladder_30_co), .S(userfulladder_27_s),
    .Co(userfulladder_27_co));
  and and_27 (and_27_out, and_76_out, and_65_out);
  and and_28 (and_28_out, and_75_out, and_68_out);
  UserFullAdder userfulladder_28 (
    .A(userfulladder_31_s), .B(and_28_out), .Ci(userfulladder_32_co), .S(userfulladder_28_s),
    .Co(userfulladder_28_co));
  and and_29 (and_29_out, and_73_out, and_69_out);
  UserFullAdder userfulladder_29 (
    .A(userfulladder_28_s), .B(and_29_out), .Ci(userhalfadder_3_c), .S(userfulladder_29_s),
    .Co(userfulladder_29_co));
  and and_30 (and_30_out, and_79_out, and_59_out);
  UserHalfAdder userhalfadder_2 (.A(userfulladder_33_co), .B(and_30_out), .S(userhalfadder_2_s), .C(userhalfadder_2_c));
  and and_31 (and_31_out, and_78_out, and_60_out);
  and and_32 (and_32_out, and_77_out, and_65_out);
  UserFullAdder userfulladder_30 (
    .A(userfulladder_34_s), .B(and_32_out), .Ci(userfulladder_35_co), .S(userfulladder_30_s),
    .Co(userfulladder_30_co));
  and and_33 (and_33_out, and_76_out, and_66_out);
  UserFullAdder userfulladder_31 (
    .A(userfulladder_30_s), .B(and_33_out), .Ci(userfulladder_36_co), .S(userfulladder_31_s),
    .Co(userfulladder_31_co));
  and and_34 (and_34_out, and_75_out, and_69_out);
  UserFullAdder userfulladder_32 (
    .A(userfulladder_36_s), .B(and_34_out), .Ci(userhalfadder_4_c), .S(userfulladder_32_s),
    .Co(userfulladder_32_co));
  and and_35 (and_35_out, and_73_out, and_70_out);
  UserHalfAdder userhalfadder_3 (.A(userfulladder_32_s), .B(and_35_out), .S(out_27), .C(userhalfadder_3_c));
  and and_36 (and_36_out, and_79_out, and_60_out);
  UserFullAdder userfulladder_33 (
    .A(and_40_out), .B(and_36_out), .Ci(userfulladder_37_co), .S(userfulladder_33_s), .Co(userfulladder_33_co));
  and and_37 (and_37_out, and_78_out, and_64_out);
  UserFullAdder userfulladder_34 (
    .A(userfulladder_33_s), .B(and_37_out), .Ci(userfulladder_38_co), .S(userfulladder_34_s),
    .Co(userfulladder_34_co));
  and and_38 (and_38_out, and_77_out, and_66_out);
  UserFullAdder userfulladder_35 (
    .A(userfulladder_38_s), .B(and_38_out), .Ci(userfulladder_39_co), .S(userfulladder_35_s),
    .Co(userfulladder_35_co));
  and and_39 (and_39_out, and_76_out, and_68_out);
  UserFullAdder userfulladder_36 (
    .A(userfulladder_35_s), .B(and_39_out), .Ci(userfulladder_40_co), .S(userfulladder_36_s),
    .Co(userfulladder_36_co));
  and and_40 (and_40_out, and_59_out, and_80_out);
  and and_41 (and_41_out, and_79_out, and_64_out);
  UserFullAdder userfulladder_37 (
    .A(and_46_out), .B(and_41_out), .Ci(userfulladder_41_co), .S(userfulladder_37_s), .Co(userfulladder_37_co));
  and and_42 (and_42_out, and_78_out, and_65_out);
  UserFullAdder userfulladder_38 (
    .A(userfulladder_37_s), .B(and_42_out), .Ci(userfulladder_42_co), .S(userfulladder_38_s),
    .Co(userfulladder_38_co));
  and and_43 (and_43_out, and_77_out, and_68_out);
  UserFullAdder userfulladder_39 (
    .A(userfulladder_42_s), .B(and_43_out), .Ci(userfulladder_43_co), .S(userfulladder_39_s),
    .Co(userfulladder_39_co));
  and and_44 (and_44_out, and_76_out, and_69_out);
  UserFullAdder userfulladder_40 (
    .A(userfulladder_39_s), .B(and_44_out), .Ci(userhalfadder_5_c), .S(userfulladder_40_s),
    .Co(userfulladder_40_co));
  and and_45 (and_45_out, and_75_out, and_70_out);
  UserHalfAdder userhalfadder_4 (.A(userfulladder_40_s), .B(and_45_out), .S(out_28), .C(userhalfadder_4_c));
  and and_46 (and_46_out, and_60_out, and_80_out);
  and and_47 (and_47_out, and_79_out, and_65_out);
  UserFullAdder userfulladder_41 (
    .A(and_50_out), .B(and_47_out), .Ci(userfulladder_44_co), .S(userfulladder_41_s), .Co(userfulladder_41_co));
  and and_48 (and_48_out, and_78_out, and_66_out);
  UserFullAdder userfulladder_42 (
    .A(userfulladder_41_s), .B(and_48_out), .Ci(userfulladder_45_co), .S(userfulladder_42_s),
    .Co(userfulladder_42_co));
  UserFullAdder userfulladder_43 (
    .A(userfulladder_45_s), .B(and_52_out), .Ci(userhalfadder_6_c), .S(userfulladder_43_s),
    .Co(userfulladder_43_co));
  and and_49 (and_49_out, and_76_out, and_70_out);
  UserHalfAdder userhalfadder_5 (.A(userfulladder_43_s), .B(and_49_out), .S(out_29), .C(userhalfadder_5_c));
  and and_50 (and_50_out, and_64_out, and_80_out);
  UserFullAdder userfulladder_44 (
    .A(and_53_out), .B(and_54_out), .Ci(userfulladder_47_co), .S(userfulladder_44_s), .Co(userfulladder_44_co));
  and and_51 (and_51_out, and_78_out, and_68_out);
  UserFullAdder userfulladder_45 (
    .A(userfulladder_44_s), .B(and_51_out), .Ci(userfulladder_46_co), .S(userfulladder_45_s),
    .Co(userfulladder_45_co));
  and and_52 (and_52_out, and_77_out, and_69_out);
  and and_53 (and_53_out, and_65_out, and_80_out);
  and and_54 (and_54_out, and_79_out, and_66_out);
  and and_55 (and_55_out, and_78_out, and_69_out);
  UserFullAdder userfulladder_46 (
    .A(userfulladder_47_s), .B(and_55_out), .Ci(userhalfadder_7_c), .S(userfulladder_46_s),
    .Co(userfulladder_46_co));
  and and_56 (and_56_out, and_77_out, and_70_out);
  UserHalfAdder userhalfadder_6 (.A(userfulladder_46_s), .B(and_56_out), .S(out_30), .C(userhalfadder_6_c));
  and and_57 (and_57_out, and_66_out, and_80_out);
  and and_58 (and_58_out, and_79_out, and_68_out);
  UserFullAdder userfulladder_47 (
    .A(and_57_out), .B(and_58_out), .Ci(userfulladder_48_co), .S(userfulladder_47_s), .Co(userfulladder_47_co));
  and and_59 (and_59_out, Enable, A7);
  and and_60 (and_60_out, Enable, A6);
  and and_61 (and_61_out, and_68_out, and_80_out);
  and and_62 (and_62_out, and_79_out, and_69_out);
  UserFullAdder userfulladder_48 (
    .A(and_61_out), .B(and_62_out), .Ci(userhalfadder_8_c), .S(userfulladder_48_s), .Co(userfulladder_48_co));
  and and_63 (and_63_out, and_78_out, and_70_out);
  UserHalfAdder userhalfadder_7 (.A(userfulladder_48_s), .B(and_63_out), .S(out_31), .C(userhalfadder_7_c));
  and and_64 (and_64_out, Enable, A5);
  and and_65 (and_65_out, Enable, A4);
  and and_66 (and_66_out, Enable, A3);
  and and_67 (and_67_out, and_79_out, and_70_out);
  UserHalfAdder userhalfadder_8 (.A(and_71_out), .B(and_67_out), .S(out_32), .C(userhalfadder_8_c));
  and and_68 (and_68_out, Enable, A2);
  and and_69 (and_69_out, Enable, A1);
  and and_70 (and_70_out, Enable, Ao);
  and and_71 (and_71_out, and_69_out, and_80_out);
  and and_72 (and_72_out, Enable, B7);
  and and_73 (and_73_out, Enable, B6);
  and and_74 (LSB, and_70_out, and_80_out);
  and and_75 (and_75_out, Enable, B5);
  and and_76 (and_76_out, Enable, B4);
  and and_77 (and_77_out, Enable, B3);
  and and_78 (and_78_out, Enable, B2);
  and and_79 (and_79_out, Enable, B1);
  and and_80 (and_80_out, Enable, Bo);
endmodule

module UserDivider (
  input  E,
  input  A7,
  input  A6,
  input  A5,
  input  A4,
  input  A3,
  input  A2,
  input  A1,
  input  Ao,
  input  B7,
  input  B6,
  input  B5,
  input  B4,
  input  B3,
  input  B2,
  input  B1,
  input  Bo,
  output LSB,
  output out_19,
  output out_20,
  output out_21,
  output out_22,
  output out_23,
  output out_24,
  output MSB
);

  wire [7:0] and_1_out, and_2_out;

  assign and_1_out = {A7, A6, A5, A4, A3, A2, A1, Ao} & {8{E}};  // AND_Gate and_1, 8 bits wide
  Divider divider_1 (
    .a(and_1_out), .b(and_2_out), .out({MSB, out_24, out_23, out_22, out_21, out_20, out_19, LSB}));  // open: upper, rem
  assign and_2_out = {B7, B6, B5, B4, B3, B2, B1, Bo} & {8{E}};  // AND_Gate and_2, 8 bits wide
endmodule

module UserBCDto7Seg (
  input  D3,
  input  D2,
  input  D1,
  input  Do,
  output g,
  output f,
  output e,
  output d,
  output c,
  output b,
  output a
);

  wire and_1_out, and_2_out, and_3_out, and_4_out, and_5_out, and_6_out, and_7_out, and_8_out, and_9_out,
       and_10_out, and_11_out, and_12_out, and_13_out, and_14_out, not_1_out, not_2_out, not_3_out, not_4_out;

  not not_1 (not_1_out, D3);
  not not_2 (not_2_out, D2);
  not not_3 (not_3_out, D1);
  not not_4 (not_4_out, Do);
  and and_1 (and_1_out, not_1_out, not_2_out, not_3_out);
  and and_2 (and_2_out, not_1_out, D2, D1, Do);
  and and_3 (and_3_out, not_1_out, not_2_out, D1);
  and and_4 (and_4_out, not_1_out, not_2_out, Do);
  and and_5 (and_5_out, not_1_out, D1, Do);
  and and_6 (and_6_out, not_1_out, D1, not_4_out);
  and and_7 (and_7_out, not_2_out, not_3_out, not_4_out);
  and and_8 (and_8_out, not_1_out, not_2_out, not_3_out, Do);
  and and_9 (and_9_out, not_1_out, D2, not_3_out, not_4_out);
  and and_10 (and_10_out, not_1_out, D2, D1, Do);
  nand nand_1 (c, not_1_out, not_2_out, D1, not_4_out);
  and and_11 (and_11_out, not_1_out, D2, not_3_out, Do);
  and and_12 (and_12_out, not_1_out, D2, D1, not_4_out);
  and and_13 (and_13_out, not_1_out, not_2_out, not_3_out, Do);
  and and_14 (and_14_out, not_1_out, D2, not_3_out, not_4_out);
  nor nor_1 (g, and_1_out, and_2_out);
  nor nor_2 (f, and_3_out, and_4_out, and_5_out);
  or or_1 (e, and_6_out, and_7_out);
  nor nor_3 (d, and_8_out, and_9_out, and_10_out);
  nor nor_4 (b, and_11_out, and_12_out);
  nor nor_5 (a, and_13_out, and_14_out);
endmodule

module User21Mux (
  input  [7:0] Ao,
  input  [7:0] A1,
  input  [7:0] S,
  output [7:0] O
);

  wire [7:0] and_1_out, and_2_out, not_1_out;

  assign not_1_out = ~S;  // NOT_Gate not_1, 8 bits wide
  assign and_1_out = S & A1;  // AND_Gate and_1, 8 bits wide
  assign and_2_out = Ao & not_1_out;  // AND_Gate and_2, 8 bits wide
  assign O = and_1_out | and_2_out;  // OR_Gate or_1, 8 bits wide
endmodule

module User2sComp (
  input  [7:0] in_1,
  output [7:0] out_2
);

  wire [7:0] not_1_out;

  assign not_1_out = ~in_1;  // NOT_Gate not_1, 8 bits wide
  Adder adder_1 (.a(not_1_out), .b(8'h1), .out(out_2), .cin(1'b0));  // open: cout
endmodule
