// Logisim project DLD_Final_With_Negative.circ as structural Verilog: 24 circuits, main circuit UserRegister8Bit
module main (
  output out_1,
  output out_2,
  output out_3,
  output out_4,
  output out_5,
  output out_6,
  output out_7,
  output out_8,
  output out_9,
  output out_10,
  output out_11,
  output out_12,
  output out_13,
  output out_14,
  output out_15,
  output out_16,
  output out_17,
  output out_18,
  output out_19,
  output out_20,
  output out_21,
  output out_22,
  output out_23,
  output out_24,
  output out_25,
  output out_26,
  output out_27,
  output out_28,
  output out_29,
  output out_30,
  output out_31,
  output out_32,
  output out_33,
  output out_34,
  output out_35,
  output out_36,
  output out_37,
  output out_38,
  output out_39,
  output out_40,
  output out_41,
  output out_42,
  output out_43,
  output out_44,
  output out_45,
  output out_46,
  output out_47,
  output out_48,
  output out_49,
  output out_50,
  output out_51,
  output out_52
);

  wire ADD_out, ALU_REG_A_w0, ALU_REG_A_w1, ALU_REG_A_w2, ALU_REG_A_w3, ALU_REG_A_w4, ALU_REG_A_w5,
       ALU_REG_A_w6, ALU_REG_A_w7, ALU_REG_B_w0, ALU_REG_B_w1, ALU_REG_B_w2, ALU_REG_B_w3, ALU_REG_B_w4,
       ALU_REG_B_w5, ALU_REG_B_w6, ALU_REG_B_w7, and_1_out, and_2_out, and_3_out, and_4_out, and_5_out,
       and_6_out, and_7_out, and_8_out, and_9_out, and_10_out, and_11_out, and_12_out, and_13_out,
       and_14_out, and_15_out, and_16_out, and_17_out, and_18_out, and_19_out, and_20_out, and_21_out,
       and_22_out, and_23_out, and_24_out, and_25_out, and_26_out, and_27_out, and_28_out, and_29_out,
       and_30_out, and_31_out, and_32_out, and_33_out, and_34_out, and_35_out, and_36_out, and_37_out,
       and_38_out, CLEAR_out, clock_1_out, controlled_buffer_1_out, controlled_buffer_2_out,
       controlled_buffer_3_out, controlled_buffer_4_out, controlled_buffer_9_out, controlled_buffer_10_out,
       controlled_buffer_11_out, controlled_buffer_12_out, DEC_o0, DEC_o1, DEC_o2, DEC_o3, DIV_out, GO_out,
       i0_out, i1_out, i2_out, i3_out, i4_out, i5_out, i6_out, i7_out, i8_out, i9_out, j_k_ff_1_q,
       j_k_ff_2_q, MUL_out, not_1_out, not_2_out, not_3_out, not_4_out, not_5_out, or_1_out, or_2_out,
       or_3_out, or_4_out, or_5_out, or_6_out, or_7_out, or_8_out, or_9_out, or_10_out, or_11_out, or_12_out,
       or_13_out, or_14_out, or_15_out, or_16_out, or_17_out, or_18_out, or_19_out, or_20_out, or_21_out,
       or_22_out, or_23_out, or_24_out, or_25_out, or_26_out, or_27_out, or_28_out, REG_A_w0, REG_A_w1,
       REG_A_w2, REG_A_w3, REG_A_w4, REG_A_w5, REG_A_w6, REG_A_w7, REG_B_w0, REG_B_w1, REG_B_w2, REG_B_w3,
       REG_B_w4, REG_B_w5, REG_B_w6, REG_B_w7, SUB_out, tmp_3_w0, tmp_3_w1, useralu_1_lsb, useralu_1_msb,
       useralu_1_negative, useralu_1_out_24, useralu_1_out_25, useralu_1_out_26, useralu_1_out_27,
       useralu_1_out_28, useralu_1_out_29, useralu_1_overflow, usercontrolunit_1_rc_0_1,
       usercontrolunit_1_rc_0_2, usercontrolunit_1_rc_0_3, usercontrolunit_1_rc_1_0,
       usercontrolunit_1_rc_1_1, usercontrolunit_1_rc_1_2, usercontrolunit_1_rc_1_3,
       usercontrolunit_1_rc_1_4, usercontrolunit_1_rc_2_1, usercontrolunit_1_rc_2_2, userencoder_4x2_1_o0,
       userencoder_4x2_1_o1, userinputencoderandtmp1_1_num_ld, userinputencoderandtmp1_1_o0,
       userinputencoderandtmp1_1_o1, userinputencoderandtmp1_1_o2, userinputencoderandtmp1_1_o3,
       userinputencoderandtmp1_1_w0, userinputencoderandtmp1_1_w1, userinputencoderandtmp1_1_w2,
       userinputencoderandtmp1_1_w3;
  wire [3:0] binary_to_bcd_converter_1_p2, binary_to_bcd_converter_1_p3, binary_to_bcd_converter_1_p4;
  wire [6:0] userbcdto7seg_1_a, userbcdto7seg_2_a, userbcdto7seg_3_a;
  wire [7:0] OUTPUT_REG_w0;

  _7_Segment_Display u_7_segment_display_1 (.g(useralu_1_negative));  // open: f, a, b, e, d, c, dp
  LED Overflow (.in(useralu_1_overflow));
  _7_Segment_Display u_7_segment_display_2 (
    .g(userbcdto7seg_1_a[6]), .f(userbcdto7seg_1_a[5]), .a(userbcdto7seg_1_a[0]), .b(userbcdto7seg_1_a[1]),
    .e(userbcdto7seg_1_a[4]), .d(userbcdto7seg_1_a[3]), .c(userbcdto7seg_1_a[2]));  // open: dp
  _7_Segment_Display u_7_segment_display_3 (
    .g(userbcdto7seg_2_a[6]), .f(userbcdto7seg_2_a[5]), .a(userbcdto7seg_2_a[0]), .b(userbcdto7seg_2_a[1]),
    .e(userbcdto7seg_2_a[4]), .d(userbcdto7seg_2_a[3]), .c(userbcdto7seg_2_a[2]));  // open: dp
  _7_Segment_Display u_7_segment_display_4 (
    .g(userbcdto7seg_3_a[6]), .f(userbcdto7seg_3_a[5]), .a(userbcdto7seg_3_a[0]), .b(userbcdto7seg_3_a[1]),
    .e(userbcdto7seg_3_a[4]), .d(userbcdto7seg_3_a[3]), .c(userbcdto7seg_3_a[2]));  // open: dp
  J_K_Flip_Flop j_k_ff_1 (
    .J(1'b1), .K(1'b1), .clk(usercontrolunit_1_rc_2_2), .Q(j_k_ff_1_q), .preset(CLEAR_out));  // open: Qn, reset
  Button i1 (.out(i1_out));
  Button i2 (.out(i2_out));
  Button i4 (.out(i4_out));
  Button i5 (.out(i5_out));
  Button i7 (.out(i7_out));
  Button i8 (.out(i8_out));
  Button ADD (.out(ADD_out));
  Button i0 (.out(i0_out));
  Button MUL (.out(MUL_out));
  Button GO (.out(GO_out));
  Button CLEAR (.out(CLEAR_out));
  and and_1 (and_1_out, j_k_ff_1_q, or_1_out);
  or or_1 (or_1_out, SUB_out, ADD_out, DIV_out, MUL_out);
  Button i3 (.out(i3_out));
  Button i6 (.out(i6_out));
  Button i9 (.out(i9_out));
  Button SUB (.out(SUB_out));
  Button DIV (.out(DIV_out));
  Clock clock_1 (.out(clock_1_out));
  and and_2 (and_2_out, not_1_out, usercontrolunit_1_rc_1_4);
  and and_3 (and_3_out, not_1_out, usercontrolunit_1_rc_1_2);
  and and_4 (and_4_out, not_1_out, usercontrolunit_1_rc_1_1);
  and and_5 (and_5_out, not_1_out, usercontrolunit_1_rc_1_0);
  not not_1 (not_1_out, j_k_ff_2_q);
  UserEncoder_4x2 userencoder_4x2_1 (
    .i3(ADD_out), .i2(SUB_out), .i1(MUL_out), .i0(DIV_out), .o1(userencoder_4x2_1_o1),
    .o0(userencoder_4x2_1_o0));
  or or_2 (or_2_out, and_2_out, and_4_out);
  or or_3 (or_3_out, and_3_out, and_5_out, usercontrolunit_1_rc_0_1);
  UserRegister8Bit tmp_3 (
    .i1(userencoder_4x2_1_o1), .i0(userencoder_4x2_1_o0), .LD(or_1_out), .CLK(clock_1_out),
    .EN(usercontrolunit_1_rc_0_3), .CLR(CLEAR_out), .Q7(out_52), .Q6(out_51), .Q5(out_50), .Q4(out_49),
    .Q3(out_48), .Q2(out_47), .W1(tmp_3_w1), .Q1(out_46), .W0(tmp_3_w0), .Q0(out_45));  // open: i7, i6, i5, i4, i3, i2, W7, W6, W5, W4, W3, W2
  UserRegister8Bit OUTPUT_REG (
    .i7(controlled_buffer_1_out), .i6(controlled_buffer_2_out), .i5(controlled_buffer_3_out),
    .i4(controlled_buffer_4_out), .i3(controlled_buffer_9_out), .i2(controlled_buffer_10_out),
    .i1(controlled_buffer_11_out), .i0(controlled_buffer_12_out), .LD(usercontrolunit_1_rc_0_3),
    .CLK(clock_1_out), .EN(1'b1), .CLR(CLEAR_out), .W7(OUTPUT_REG_w0[7]), .Q7(out_1), .W6(OUTPUT_REG_w0[6]),
    .Q6(out_2), .W5(OUTPUT_REG_w0[5]), .Q5(out_3), .W4(OUTPUT_REG_w0[4]), .Q4(out_4), .W3(OUTPUT_REG_w0[3]),
    .Q3(out_5), .W2(OUTPUT_REG_w0[2]), .Q2(out_6), .W1(OUTPUT_REG_w0[1]), .Q1(out_7), .W0(OUTPUT_REG_w0[0]),
    .Q0(out_8));
  UserControlUnit usercontrolunit_1 (
    .rc_2(and_1_out), .rc_1(userinputencoderandtmp1_1_num_ld), .rc_0(GO_out), .CLK(clock_1_out),
    .rc_2_2(usercontrolunit_1_rc_2_2), .rc_2_1(usercontrolunit_1_rc_2_1), .rc_1_4(usercontrolunit_1_rc_1_4),
    .rc_1_3(usercontrolunit_1_rc_1_3), .rc_1_2(usercontrolunit_1_rc_1_2), .rc_1_1(usercontrolunit_1_rc_1_1),
    .rc_1_0(usercontrolunit_1_rc_1_0), .rc_0_3(usercontrolunit_1_rc_0_3), .rc_0_2(usercontrolunit_1_rc_0_2),
    .rc_0_1(usercontrolunit_1_rc_0_1));  // open: rc_2_0, rc_0_0
  // Binary_to_BCD_converter #(.binvalue(8)) binary_to_bcd_converter_1: pin names not known; wires that end beside it: OUTPUT_REG_w0, binary_to_bcd_converter_1_p2, binary_to_bcd_converter_1_p3, binary_to_bcd_converter_1_p4
  UserRegister8Bit REG_A (
    .i7(controlled_buffer_1_out), .i6(controlled_buffer_2_out), .i5(controlled_buffer_3_out),
    .i4(controlled_buffer_4_out), .i3(controlled_buffer_9_out), .i2(controlled_buffer_10_out),
    .i1(controlled_buffer_11_out), .i0(controlled_buffer_12_out), .LD(or_2_out), .CLK(clock_1_out),
    .EN(or_3_out), .CLR(CLEAR_out), .W7(REG_A_w7), .Q7(out_32), .W6(REG_A_w6), .Q6(out_31), .W5(REG_A_w5),
    .Q5(out_30), .W4(REG_A_w4), .Q4(out_29), .W3(REG_A_w3), .Q3(out_28), .W2(REG_A_w2), .Q2(out_27),
    .W1(REG_A_w1), .Q1(out_26), .W0(REG_A_w0), .Q0(out_25));
  J_K_Flip_Flop j_k_ff_2 (
    .J(1'b1), .K(1'b1), .clk(usercontrolunit_1_rc_2_1), .Q(j_k_ff_2_q), .reset(CLEAR_out));  // open: Qn, preset
  UserInputEncoderAndTmp1 userinputencoderandtmp1_1 (
    .i1(i1_out), .i2(i2_out), .i3(i3_out), .i4(i4_out), .i5(i5_out), .i6(i6_out), .CLK(clock_1_out),
    .EN(usercontrolunit_1_rc_1_3), .CLR(CLEAR_out), .i7(i7_out), .i8(i8_out), .i9(i9_out), .i0(i0_out),
    .NUM_LD(userinputencoderandtmp1_1_num_ld), .o3(userinputencoderandtmp1_1_o3),
    .o2(userinputencoderandtmp1_1_o2), .o1(userinputencoderandtmp1_1_o1), .o0(userinputencoderandtmp1_1_o0),
    .W3(userinputencoderandtmp1_1_w3), .Q3(out_41), .W2(userinputencoderandtmp1_1_w2), .Q2(out_42),
    .W1(userinputencoderandtmp1_1_w1), .Q1(out_43), .W0(userinputencoderandtmp1_1_w0), .Q0(out_44));
  LED led_1 (.in(userinputencoderandtmp1_1_o3));
  LED led_2 (.in(userinputencoderandtmp1_1_o2));
  LED led_3 (.in(userinputencoderandtmp1_1_o1));
  LED led_4 (.in(userinputencoderandtmp1_1_o0));
  and and_6 (and_6_out, j_k_ff_2_q, usercontrolunit_1_rc_1_4);
  and and_7 (and_7_out, j_k_ff_2_q, usercontrolunit_1_rc_1_1);
  and and_8 (and_8_out, j_k_ff_2_q, usercontrolunit_1_rc_1_0);
  and and_9 (and_9_out, j_k_ff_2_q, usercontrolunit_1_rc_1_2);
  assign controlled_buffer_1_out = usercontrolunit_1_rc_1_3 ? 1'b0 : 1'bz;  // Controlled_Buffer controlled_buffer_1
  assign controlled_buffer_2_out = usercontrolunit_1_rc_1_3 ? 1'b0 : 1'bz;  // Controlled_Buffer controlled_buffer_2
  assign controlled_buffer_3_out = usercontrolunit_1_rc_1_3 ? 1'b0 : 1'bz;  // Controlled_Buffer controlled_buffer_3
  assign controlled_buffer_4_out = usercontrolunit_1_rc_1_3 ? 1'b0 : 1'bz;  // Controlled_Buffer controlled_buffer_4
  assign controlled_buffer_1_out = or_3_out ? REG_A_w7 : 1'bz;  // Controlled_Buffer controlled_buffer_5
  assign controlled_buffer_2_out = or_3_out ? REG_A_w6 : 1'bz;  // Controlled_Buffer controlled_buffer_6
  assign controlled_buffer_3_out = or_3_out ? REG_A_w5 : 1'bz;  // Controlled_Buffer controlled_buffer_7
  assign controlled_buffer_4_out = or_3_out ? REG_A_w4 : 1'bz;  // Controlled_Buffer controlled_buffer_8
  assign controlled_buffer_9_out = or_3_out ? REG_A_w3 : 1'bz;  // Controlled_Buffer controlled_buffer_9
  assign controlled_buffer_10_out = or_3_out ? REG_A_w2 : 1'bz;  // Controlled_Buffer controlled_buffer_10
  assign controlled_buffer_11_out = or_3_out ? REG_A_w1 : 1'bz;  // Controlled_Buffer controlled_buffer_11
  assign controlled_buffer_12_out = or_3_out ? REG_A_w0 : 1'bz;  // Controlled_Buffer controlled_buffer_12
  or or_4 (or_4_out, and_6_out, and_7_out);
  or or_5 (or_5_out, and_8_out, usercontrolunit_1_rc_0_2, and_9_out);
  UserBCDto7Seg userbcdto7seg_1 (
    .D3(binary_to_bcd_converter_1_p2[3]), .D2(binary_to_bcd_converter_1_p2[2]),
    .D1(binary_to_bcd_converter_1_p2[1]), .Do(binary_to_bcd_converter_1_p2[0]), .g(userbcdto7seg_1_a[6]),
    .f(userbcdto7seg_1_a[5]), .e(userbcdto7seg_1_a[4]), .d(userbcdto7seg_1_a[3]), .c(userbcdto7seg_1_a[2]),
    .b(userbcdto7seg_1_a[1]), .a(userbcdto7seg_1_a[0]));
  assign controlled_buffer_9_out = usercontrolunit_1_rc_1_3 ? userinputencoderandtmp1_1_w3 : 1'bz;  // Controlled_Buffer controlled_buffer_13
  assign controlled_buffer_10_out = usercontrolunit_1_rc_1_3 ? userinputencoderandtmp1_1_w2 : 1'bz;  // Controlled_Buffer controlled_buffer_14
  assign controlled_buffer_11_out = usercontrolunit_1_rc_1_3 ? userinputencoderandtmp1_1_w1 : 1'bz;  // Controlled_Buffer controlled_buffer_15
  or or_6 (or_6_out, DEC_o0, or_7_out, DEC_o2, or_8_out);
  assign controlled_buffer_12_out = usercontrolunit_1_rc_1_3 ? userinputencoderandtmp1_1_w0 : 1'bz;  // Controlled_Buffer controlled_buffer_16
  UserBCDto7Seg userbcdto7seg_2 (
    .D3(binary_to_bcd_converter_1_p3[3]), .D2(binary_to_bcd_converter_1_p3[2]),
    .D1(binary_to_bcd_converter_1_p3[1]), .Do(binary_to_bcd_converter_1_p3[0]), .g(userbcdto7seg_2_a[6]),
    .f(userbcdto7seg_2_a[5]), .e(userbcdto7seg_2_a[4]), .d(userbcdto7seg_2_a[3]), .c(userbcdto7seg_2_a[2]),
    .b(userbcdto7seg_2_a[1]), .a(userbcdto7seg_2_a[0]));
  assign controlled_buffer_1_out = or_6_out ? useralu_1_msb : 1'bz;  // Controlled_Buffer controlled_buffer_17
  UserALU useralu_1 (
    .ADD(or_8_out), .SUB(DEC_o2), .MUL(or_7_out), .DIV(DEC_o0), .A7(or_9_out), .A6(or_10_out),
    .A5(or_11_out), .A4(or_12_out), .A3(or_13_out), .A2(or_14_out), .A1(or_17_out), .Ao(or_18_out),
    .B7(or_19_out), .B6(or_20_out), .B5(or_21_out), .B4(or_22_out), .B3(or_23_out), .B2(or_24_out),
    .B1(or_25_out), .Bo(or_27_out), .OVERFLOW(useralu_1_overflow), .Negative(useralu_1_negative),
    .MSB(useralu_1_msb), .out_24(useralu_1_out_24), .out_25(useralu_1_out_25), .out_26(useralu_1_out_26),
    .out_27(useralu_1_out_27), .out_28(useralu_1_out_28), .out_29(useralu_1_out_29), .LSB(useralu_1_lsb));
  or or_7 (or_7_out, usercontrolunit_1_rc_1_1, DEC_o1);
  or or_8 (or_8_out, usercontrolunit_1_rc_1_4, DEC_o3);
  UserDecoder_2x4 DEC (
    .i1(tmp_3_w1), .i0(tmp_3_w0), .EN(usercontrolunit_1_rc_0_3), .o3(DEC_o3), .o2(DEC_o2), .o1(DEC_o1),
    .o0(DEC_o0));
  not not_2 (not_2_out, 1'b1);
  assign controlled_buffer_12_out = or_5_out ? REG_B_w0 : 1'bz;  // Controlled_Buffer controlled_buffer_18
  assign controlled_buffer_11_out = or_5_out ? REG_B_w1 : 1'bz;  // Controlled_Buffer controlled_buffer_19
  assign controlled_buffer_10_out = or_5_out ? REG_B_w2 : 1'bz;  // Controlled_Buffer controlled_buffer_20
  assign controlled_buffer_9_out = or_5_out ? REG_B_w3 : 1'bz;  // Controlled_Buffer controlled_buffer_21
  assign controlled_buffer_4_out = or_5_out ? REG_B_w4 : 1'bz;  // Controlled_Buffer controlled_buffer_22
  assign controlled_buffer_3_out = or_5_out ? REG_B_w5 : 1'bz;  // Controlled_Buffer controlled_buffer_23
  assign controlled_buffer_2_out = or_5_out ? REG_B_w6 : 1'bz;  // Controlled_Buffer controlled_buffer_24
  assign controlled_buffer_1_out = or_5_out ? REG_B_w7 : 1'bz;  // Controlled_Buffer controlled_buffer_25
  assign controlled_buffer_2_out = or_6_out ? useralu_1_out_24 : 1'bz;  // Controlled_Buffer controlled_buffer_26
  assign controlled_buffer_3_out = or_6_out ? useralu_1_out_25 : 1'bz;  // Controlled_Buffer controlled_buffer_27
  assign controlled_buffer_4_out = or_6_out ? useralu_1_out_26 : 1'bz;  // Controlled_Buffer controlled_buffer_28
  assign controlled_buffer_9_out = or_6_out ? useralu_1_out_27 : 1'bz;  // Controlled_Buffer controlled_buffer_29
  not not_3 (not_3_out, not_4_out);
  and and_10 (and_10_out, not_2_out, usercontrolunit_1_rc_1_1);
  and and_11 (and_11_out, 1'b1, usercontrolunit_1_rc_1_1);
  and and_12 (and_12_out, ~1'b1, usercontrolunit_1_rc_1_1);  // AND_Gate
  and and_13 (and_13_out, 1'b1, usercontrolunit_1_rc_1_1);
  and and_14 (and_14_out, ~1'b1, usercontrolunit_1_rc_1_1);  // AND_Gate
  UserBCDto7Seg userbcdto7seg_3 (
    .D3(binary_to_bcd_converter_1_p4[3]), .D2(binary_to_bcd_converter_1_p4[2]),
    .D1(binary_to_bcd_converter_1_p4[1]), .Do(binary_to_bcd_converter_1_p4[0]), .g(userbcdto7seg_3_a[6]),
    .f(userbcdto7seg_3_a[5]), .e(userbcdto7seg_3_a[4]), .d(userbcdto7seg_3_a[3]), .c(userbcdto7seg_3_a[2]),
    .b(userbcdto7seg_3_a[1]), .a(userbcdto7seg_3_a[0]));
  assign controlled_buffer_10_out = or_6_out ? useralu_1_out_28 : 1'bz;  // Controlled_Buffer controlled_buffer_30
  assign controlled_buffer_11_out = or_6_out ? useralu_1_out_29 : 1'bz;  // Controlled_Buffer controlled_buffer_31
  assign controlled_buffer_12_out = or_6_out ? useralu_1_lsb : 1'bz;  // Controlled_Buffer controlled_buffer_32
  or or_9 (or_9_out, and_15_out, ALU_REG_A_w7);
  or or_10 (or_10_out, and_16_out, ALU_REG_A_w6);
  and and_15 (and_15_out, and_10_out, not_3_out);
  and and_16 (and_16_out, and_10_out, not_3_out);
  UserRegister8Bit ALU_REG_A (
    .i7(controlled_buffer_1_out), .i6(controlled_buffer_2_out), .i5(controlled_buffer_3_out),
    .i4(controlled_buffer_4_out), .i3(controlled_buffer_9_out), .i2(controlled_buffer_10_out),
    .i1(controlled_buffer_11_out), .i0(controlled_buffer_12_out), .LD(or_15_out), .CLK(clock_1_out),
    .EN(or_16_out), .CLR(CLEAR_out), .W7(ALU_REG_A_w7), .Q7(out_9), .W6(ALU_REG_A_w6), .Q6(out_10),
    .W5(ALU_REG_A_w5), .Q5(out_11), .W4(ALU_REG_A_w4), .Q4(out_12), .W3(ALU_REG_A_w3), .Q3(out_13),
    .W2(ALU_REG_A_w2), .Q2(out_14), .W1(ALU_REG_A_w1), .Q1(out_15), .W0(ALU_REG_A_w0), .Q0(out_16));
  and and_17 (and_17_out, not_4_out, usercontrolunit_1_rc_1_2);
  or or_11 (or_11_out, and_18_out, ALU_REG_A_w5);
  or or_12 (or_12_out, and_19_out, ALU_REG_A_w4);
  and and_18 (and_18_out, and_10_out, not_3_out);
  and and_19 (and_19_out, and_10_out, not_3_out);
  and and_20 (and_20_out, j_k_ff_2_q, usercontrolunit_1_rc_1_3);
  or or_13 (or_13_out, and_21_out, ALU_REG_A_w3);
  or or_14 (or_14_out, and_22_out, ALU_REG_A_w2);
  and and_21 (and_21_out, and_11_out, not_3_out);
  and and_22 (and_22_out, and_12_out, not_3_out);
  or or_15 (or_15_out, usercontrolunit_1_rc_0_1, and_17_out, and_23_out, and_20_out);
  or or_16 (or_16_out, usercontrolunit_1_rc_0_3, and_24_out, usercontrolunit_1_rc_1_4);
  and and_23 (and_23_out, not_4_out, usercontrolunit_1_rc_1_0);
  and and_24 (and_24_out, not_4_out, usercontrolunit_1_rc_1_1);
  not not_4 (not_4_out, j_k_ff_2_q);
  UserRegister8Bit REG_B (
    .i7(controlled_buffer_1_out), .i6(controlled_buffer_2_out), .i5(controlled_buffer_3_out),
    .i4(controlled_buffer_4_out), .i3(controlled_buffer_9_out), .i2(controlled_buffer_10_out),
    .i1(controlled_buffer_11_out), .i0(controlled_buffer_12_out), .LD(or_4_out), .CLK(clock_1_out),
    .EN(or_5_out), .CLR(CLEAR_out), .W7(REG_B_w7), .Q7(out_40), .W6(REG_B_w6), .Q6(out_39), .W5(REG_B_w5),
    .Q5(out_38), .W4(REG_B_w4), .Q4(out_37), .W3(REG_B_w3), .Q3(out_36), .W2(REG_B_w2), .Q2(out_35),
    .W1(REG_B_w1), .Q1(out_34), .W0(REG_B_w0), .Q0(out_33));
  or or_17 (or_17_out, and_25_out, ALU_REG_A_w1);
  or or_18 (or_18_out, and_26_out, ALU_REG_A_w0);
  and and_25 (and_25_out, and_13_out, not_3_out);
  and and_26 (and_26_out, and_14_out, not_3_out);
  or or_19 (or_19_out, and_27_out, ALU_REG_B_w7);
  and and_27 (and_27_out, and_10_out, not_4_out);
  or or_20 (or_20_out, and_28_out, ALU_REG_B_w6);
  or or_21 (or_21_out, and_29_out, ALU_REG_B_w5);
  and and_28 (and_28_out, and_10_out, not_4_out);
  and and_29 (and_29_out, and_10_out, not_4_out);
  UserRegister8Bit ALU_REG_B (
    .i7(controlled_buffer_1_out), .i6(controlled_buffer_2_out), .i5(controlled_buffer_3_out),
    .i4(controlled_buffer_4_out), .i3(controlled_buffer_9_out), .i2(controlled_buffer_10_out),
    .i1(controlled_buffer_11_out), .i0(controlled_buffer_12_out), .LD(or_26_out), .CLK(clock_1_out),
    .EN(or_28_out), .CLR(CLEAR_out), .W7(ALU_REG_B_w7), .Q7(out_17), .W6(ALU_REG_B_w6), .Q6(out_18),
    .W5(ALU_REG_B_w5), .Q5(out_19), .W4(ALU_REG_B_w4), .Q4(out_20), .W3(ALU_REG_B_w3), .Q3(out_21),
    .W2(ALU_REG_B_w2), .Q2(out_22), .W1(ALU_REG_B_w1), .Q1(out_23), .W0(ALU_REG_B_w0), .Q0(out_24));
  or or_22 (or_22_out, and_30_out, ALU_REG_B_w4);
  or or_23 (or_23_out, and_31_out, ALU_REG_B_w3);
  and and_30 (and_30_out, and_10_out, not_4_out);
  and and_31 (and_31_out, and_11_out, not_4_out);
  not not_5 (not_5_out, j_k_ff_2_q);
  or or_24 (or_24_out, and_32_out, ALU_REG_B_w2);
  or or_25 (or_25_out, and_33_out, ALU_REG_B_w1);
  and and_32 (and_32_out, and_12_out, not_4_out);
  and and_33 (and_33_out, and_13_out, not_4_out);
  or or_26 (or_26_out, usercontrolunit_1_rc_0_2, and_34_out, and_35_out, and_38_out);
  and and_34 (and_34_out, not_5_out, usercontrolunit_1_rc_1_3);
  and and_35 (and_35_out, j_k_ff_2_q, usercontrolunit_1_rc_1_0);
  or or_27 (or_27_out, and_36_out, ALU_REG_B_w0);
  and and_36 (and_36_out, and_14_out, not_4_out);
  or or_28 (or_28_out, usercontrolunit_1_rc_0_3, usercontrolunit_1_rc_1_4, and_37_out);
  and and_37 (and_37_out, j_k_ff_2_q, usercontrolunit_1_rc_1_1);
  and and_38 (and_38_out, usercontrolunit_1_rc_1_2, j_k_ff_2_q);
endmodule

module UserRegister8Bit (
  input  i7,
  input  i6,
  input  i5,
  input  i4,
  input  i3,
  input  i2,
  input  i1,
  input  i0,
  input  LD,
  input  CLK,
  input  EN,
  input  CLR,
  output W7,
  output Q7,
  output W6,
  output Q6,
  output W5,
  output Q5,
  output W4,
  output Q4,
  output W3,
  output Q3,
  output W2,
  output Q2,
  output W1,
  output Q1,
  output W0,
  output Q0
);

  UserDFlipFlop userdflipflop_1 (.INP(i7), .LD(LD), .CLK(CLK), .EN(EN), .CLR(CLR), .W(W7), .Q(Q7));
  UserDFlipFlop userdflipflop_2 (.INP(i6), .LD(LD), .CLK(CLK), .EN(EN), .CLR(CLR), .W(W6), .Q(Q6));
  UserDFlipFlop userdflipflop_3 (.INP(i5), .LD(LD), .CLK(CLK), .EN(EN), .CLR(CLR), .W(W5), .Q(Q5));
  UserDFlipFlop userdflipflop_4 (.INP(i4), .LD(LD), .CLK(CLK), .EN(EN), .CLR(CLR), .W(W4), .Q(Q4));
  UserDFlipFlop userdflipflop_5 (.INP(i3), .LD(LD), .CLK(CLK), .EN(EN), .CLR(CLR), .W(W3), .Q(Q3));
  UserDFlipFlop userdflipflop_6 (.INP(i2), .LD(LD), .CLK(CLK), .EN(EN), .CLR(CLR), .W(W2), .Q(Q2));
  UserDFlipFlop userdflipflop_7 (.INP(i1), .LD(LD), .CLK(CLK), .EN(EN), .CLR(CLR), .W(W1), .Q(Q1));
  UserDFlipFlop userdflipflop_8 (.INP(i0), .LD(LD), .CLK(CLK), .EN(EN), .CLR(CLR), .W(W0), .Q(Q0));
endmodule

module UserDLatch (
  input  INP,
  input  LD,
  input  CLK,
  input  CLR,
  input  PRS,
  input  EN,
  output W,
  output Q
);

  wire and_1_out, and_2_out, and_3_out, nand_1_out, nand_2_out, nand_4_out, not_1_out, not_2_out, not_3_out;

  and and_1 (and_1_out, CLK, LD);
  not not_1 (not_1_out, INP);
  nand nand_1 (nand_1_out, INP, and_1_out);
  nand nand_2 (nand_2_out, and_1_out, not_1_out);
  not not_2 (not_2_out, CLR);
  not not_3 (not_3_out, PRS);
  and and_2 (and_2_out, nand_1_out, not_3_out);
  and and_3 (and_3_out, not_2_out, nand_2_out);
  nand nand_3 (Q, and_2_out, nand_4_out);
  nand nand_4 (nand_4_out, Q, and_3_out);
  and and_4 (W, EN, Q);
endmodule

module UserNormalCounter (
  input  COUNT,
  input  CLK,
  input  CLR,
  output c3,
  output c2,
  output c1,
  output c0
);

  wire not_1_out, not_2_out, not_3_out, not_4_out;

  not not_1 (not_1_out, CLK);
  J_K_Flip_Flop j_k_ff_1 (.J(COUNT), .K(COUNT), .clk(not_1_out), .Q(c0), .reset(CLR));  // open: Qn, preset
  J_K_Flip_Flop j_k_ff_2 (.J(COUNT), .K(COUNT), .clk(not_2_out), .Q(c1), .reset(CLR));  // open: Qn, preset
  not not_2 (not_2_out, c0);
  J_K_Flip_Flop j_k_ff_3 (.J(COUNT), .K(COUNT), .clk(not_3_out), .Q(c2), .reset(CLR));  // open: Qn, preset
  not not_3 (not_3_out, c1);
  J_K_Flip_Flop j_k_ff_4 (.J(COUNT), .K(COUNT), .clk(not_4_out), .Q(c3), .reset(CLR));  // open: Qn, preset
  not not_4 (not_4_out, c2);
endmodule

module UserRingCounter4 (
  input  PULSE,
  input  CLK,
  output o3,
  output o2,
  output o1,
  output o0
);

  wire d_ff_1_q, d_ff_6_q, j_k_ff_1_q, or_1_out, or_2_out;

  or or_1 (or_1_out, PULSE, d_ff_6_q);
  J_K_Flip_Flop j_k_ff_1 (.J(1'b1), .K(1'b1), .clk(or_1_out), .Q(j_k_ff_1_q));  // open: Qn, preset, reset
  D_Flip_Flop d_ff_1 (.D(d_ff_6_q), .clk(CLK), .Q(d_ff_1_q), .preset(or_1_out), .reset(j_k_ff_1_q));  // open: Qn
  or or_2 (or_2_out, j_k_ff_1_q, or_1_out);
  D_Flip_Flop d_ff_2 (.D(d_ff_1_q), .clk(CLK), .Q(o0), .reset(or_2_out));  // open: Qn, preset
  D_Flip_Flop d_ff_3 (.D(o0), .clk(CLK), .Q(o1), .reset(or_2_out));  // open: Qn, preset
  D_Flip_Flop d_ff_4 (.D(o1), .clk(CLK), .Q(o2), .reset(or_2_out));  // open: Qn, preset
  D_Flip_Flop d_ff_5 (.D(o2), .clk(CLK), .Q(o3), .reset(or_2_out));  // open: Qn, preset
  D_Flip_Flop d_ff_6 (.D(o3), .clk(CLK), .Q(d_ff_6_q), .reset(or_2_out));  // open: Qn, preset
endmodule

module UserInputEncoderAndTmp1 (
  input  i1,
  input  i2,
  input  i3,
  input  i4,
  input  i5,
  input  i6,
  input  CLK,
  input  EN,
  input  CLR,
  input  i7,
  input  i8,
  input  i9,
  input  i0,
  output NUM_LD,
  output o3,
  output o2,
  output o1,
  output o0,
  output W3,
  output Q3,
  output W2,
  output Q2,
  output W1,
  output Q1,
  output W0,
  output Q0
);

  or or_1 (o3, i8, i9);
  or or_2 (o2, i7, i6, i5, i4);
  or or_3 (o1, i7, i6, i3, i2);
  or or_4 (o0, i7, i5, i9, i3, i1);
  or or_5 (NUM_LD, i3, i2, i1, i4, i6, i5, i9, i8, i7, i0);
  UserRegister8Bit userregister8bit_1 (
    .i3(o3), .i2(o2), .i1(o1), .i0(o0), .LD(NUM_LD), .CLK(CLK), .EN(EN), .CLR(CLR), .W3(W3), .Q3(Q3),
    .W2(W2), .Q2(Q2), .W1(W1), .Q1(Q1), .W0(W0), .Q0(Q0));  // open: i7, i6, i5, i4, W7, Q7, W6, Q6, W5, Q5, W4, Q4
endmodule

module UserDFlipFlop (
  input  INP,
  input  LD,
  input  CLK,
  input  EN,
  input  CLR,
  output W,
  output Q
);

  wire and_1_out, and_2_out, nand_1_out, nand_2_out, nand_3_out, nand_4_out, nand_5_out, nand_6_out,
       nand_8_out, not_1_out, not_2_out, not_3_out, not_4_out;

  and and_1 (and_1_out, CLK, LD);
  not not_1 (not_1_out, INP);
  not not_2 (not_2_out, and_1_out);
  nand nand_1 (nand_1_out, INP, not_2_out);
  nand nand_2 (nand_2_out, not_2_out, not_1_out);
  nand nand_3 (nand_3_out, nand_1_out, nand_4_out);
  nand nand_4 (nand_4_out, nand_3_out, nand_2_out);
  not not_3 (not_3_out, CLR);
  not not_4 (not_4_out, nand_3_out);
  nand nand_5 (nand_5_out, nand_3_out, and_1_out);
  nand nand_6 (nand_6_out, and_1_out, not_4_out);
  and and_2 (and_2_out, nand_6_out, not_3_out);
  nand nand_7 (Q, nand_5_out, nand_8_out);
  nand nand_8 (nand_8_out, Q, and_2_out);
  and and_3 (W, EN, Q);
endmodule

module UserALU (
  input  ADD,
  input  SUB,
  input  MUL,
  input  DIV,
  input  A7,
  input  A6,
  input  A5,
  input  A4,
  input  A3,
  input  A2,
  input  A1,
  input  Ao,
  input  B7,
  input  B6,
  input  B5,
  input  B4,
  input  B3,
  input  B2,
  input  B1,
  input  Bo,
  output OVERFLOW,
  output Negative,
  output MSB,
  output out_24,
  output out_25,
  output out_26,
  output out_27,
  output out_28,
  output out_29,
  output LSB
);

  wire or_1_out, useraddandsub_1_lsb, useraddandsub_1_msb, useraddandsub_1_neglect, useraddandsub_1_out_22,
       useraddandsub_1_out_23, useraddandsub_1_out_24, useraddandsub_1_out_25, useraddandsub_1_out_26,
       useraddandsub_1_out_27, userdivider_1_lsb, userdivider_1_msb, userdivider_1_out_19,
       userdivider_1_out_20, userdivider_1_out_21, userdivider_1_out_22, userdivider_1_out_23,
       userdivider_1_out_24, usermultiplier_1_lsb, usermultiplier_1_msb, usermultiplier_1_out_19,
       usermultiplier_1_out_20, usermultiplier_1_out_21, usermultiplier_1_out_22, usermultiplier_1_out_23,
       usermultiplier_1_out_24, usermultiplier_1_out_25, usermultiplier_1_out_26, usermultiplier_1_out_27,
       usermultiplier_1_out_28, usermultiplier_1_out_29, usermultiplier_1_out_30, usermultiplier_1_out_31,
       usermultiplier_1_out_32;

  or or_1 (or_1_out, ADD, SUB);
  UserAddAndSub useraddandsub_1 (
    .SubtractionBit(SUB), .Enable(or_1_out), .Bo(Bo), .B1(B1), .B2(B2), .B3(B3), .B4(B4), .B5(B5), .B6(B6),
    .B7(B7), .Ao(Ao), .A1(A1), .A2(A2), .A3(A3), .A4(A4), .A5(A5), .A6(A6), .A7(A7),
    .LSB(useraddandsub_1_lsb), .neglect(useraddandsub_1_neglect), .NegativeSign(Negative),
    .MSB(useraddandsub_1_msb), .out_22(useraddandsub_1_out_22), .out_23(useraddandsub_1_out_23),
    .out_24(useraddandsub_1_out_24), .out_25(useraddandsub_1_out_25), .out_26(useraddandsub_1_out_26),
    .out_27(useraddandsub_1_out_27));
  UserDivider userdivider_1 (
    .E(DIV), .A7(A7), .A6(A6), .A5(A5), .A4(A4), .A3(A3), .A2(A2), .A1(A1), .Ao(Ao), .B7(B7), .B6(B6),
    .B5(B5), .B4(B4), .B3(B3), .B2(B2), .B1(B1), .Bo(Bo), .LSB(userdivider_1_lsb),
    .out_19(userdivider_1_out_19), .out_20(userdivider_1_out_20), .out_21(userdivider_1_out_21),
    .out_22(userdivider_1_out_22), .out_23(userdivider_1_out_23), .out_24(userdivider_1_out_24),
    .MSB(userdivider_1_msb));
  or or_2 (OVERFLOW, useraddandsub_1_neglect, usermultiplier_1_msb, usermultiplier_1_out_19, usermultiplier_1_out_20, usermultiplier_1_out_21, usermultiplier_1_out_22, usermultiplier_1_out_23, usermultiplier_1_out_24, usermultiplier_1_out_25);
  UserMultiplier usermultiplier_1 (
    .Enable(MUL), .A7(A7), .A6(A6), .A5(A5), .A4(A4), .A3(A3), .A2(A2), .A1(A1), .Ao(Ao), .B7(B7), .B6(B6),
    .B5(B5), .B4(B4), .B3(B3), .B2(B2), .B1(B1), .Bo(Bo), .MSB(usermultiplier_1_msb),
    .out_19(usermultiplier_1_out_19), .out_20(usermultiplier_1_out_20), .out_21(usermultiplier_1_out_21),
    .out_22(usermultiplier_1_out_22), .out_23(usermultiplier_1_out_23), .out_24(usermultiplier_1_out_24),
    .out_25(usermultiplier_1_out_25), .out_26(usermultiplier_1_out_26), .out_27(usermultiplier_1_out_27),
    .out_28(usermultiplier_1_out_28), .out_29(usermultiplier_1_out_29), .out_30(usermultiplier_1_out_30),
    .out_31(usermultiplier_1_out_31), .out_32(usermultiplier_1_out_32), .LSB(usermultiplier_1_lsb));
  or or_3 (MSB, useraddandsub_1_msb, usermultiplier_1_out_26, userdivider_1_msb);
  or or_4 (out_24, useraddandsub_1_out_22, usermultiplier_1_out_27, userdivider_1_out_24);
  or or_5 (out_25, useraddandsub_1_out_23, usermultiplier_1_out_28, userdivider_1_out_23);
  or or_6 (out_26, useraddandsub_1_out_24, usermultiplier_1_out_29, userdivider_1_out_22);
  or or_7 (out_27, useraddandsub_1_out_25, usermultiplier_1_out_30, userdivider_1_out_21);
  or or_8 (out_28, useraddandsub_1_out_26, usermultiplier_1_out_31, userdivider_1_out_20);
  or or_9 (out_29, useraddandsub_1_out_27, usermultiplier_1_out_32, userdivider_1_out_19);
  or or_10 (LSB, useraddandsub_1_lsb, usermultiplier_1_lsb, userdivider_1_lsb);
endmodule

module UserHalfAdder (
  input  A,
  input  B,
  output S,
  output C
);

  xor xor_1 (S, A, B);
  and and_1 (C, A, B);
endmodule

module UserFullAdder (
  input  Ci,
  input  A,
  input  B,
  output S,
  output Co
);

  wire and_1_out, and_2_out, xor_1_out;

  xor xor_1 (xor_1_out, A, B);
  and and_1 (and_1_out, A, B);
  xor xor_2 (S, Ci, xor_1_out);
  and and_2 (and_2_out, Ci, xor_1_out);
  or or_1 (Co, and_1_out, and_2_out);
endmodule

module UserAddAndSub (
  input  Enable,
  input  Ao,
  input  A1,
  input  A2,
  input  A3,
  input  A4,
  input  A5,
  input  A6,
  input  A7,
  input  SubtractionBit,
  input  Bo,
  input  B1,
  input  B2,
  input  B3,
  input  B4,
  input  B5,
  input  B6,
  input  B7,
  output neglect,
  output NegativeSign,
  output MSB,
  output out_22,
  output out_23,
  output out_24,
  output out_25,
  output out_26,
  output out_27,
  output LSB
);

  wire and_1_out, and_2_out, and_3_out, and_4_out, and_5_out, and_6_out, and_7_out, and_8_out, and_9_out,
       and_10_out, and_11_out, and_12_out, and_13_out, and_14_out, and_15_out, and_16_out,
       userfulladder_1_co, userfulladder_2_co, userfulladder_3_co, userfulladder_4_co, userfulladder_5_co,
       userfulladder_6_co, userfulladder_7_co, xor_1_out, xor_2_out, xor_3_out, xor_4_out, xor_5_out,
       xor_6_out, xor_7_out, xor_8_out;
  wire [7:0] user2scomp_1_out_2, userfulladder_1_s;

  and and_1 (and_1_out, Enable, Bo);
  and and_2 (and_2_out, Enable, B1);
  and and_3 (and_3_out, Enable, B2);
  and and_4 (and_4_out, Enable, B3);
  and and_5 (and_5_out, Enable, B4);
  and and_6 (and_6_out, Enable, B5);
  and and_7 (and_7_out, Enable, B6);
  and and_8 (and_8_out, Enable, B7);
  and and_9 (and_9_out, Enable, Ao);
  and and_10 (and_10_out, Enable, A1);
  and and_11 (and_11_out, Enable, A2);
  and and_12 (and_12_out, Enable, A3);
  and and_13 (and_13_out, Enable, A4);
  and and_14 (and_14_out, Enable, A5);
  and and_15 (and_15_out, Enable, A6);
  and and_16 (and_16_out, Enable, A7);
  xor xor_1 (xor_1_out, SubtractionBit, and_1_out);
  xor xor_2 (xor_2_out, SubtractionBit, and_2_out);
  xor xor_3 (xor_3_out, SubtractionBit, and_3_out);
  xor xor_4 (xor_4_out, SubtractionBit, and_4_out);
  xor xor_5 (xor_5_out, SubtractionBit, and_5_out);
  xor xor_6 (xor_6_out, SubtractionBit, and_6_out);
  xor xor_7 (xor_7_out, SubtractionBit, and_7_out);
  xor xor_8 (xor_8_out, SubtractionBit, and_8_out);
  UserFullAdder userfulladder_1 (
    .A(and_9_out), .B(xor_1_out), .Ci(SubtractionBit), .S(userfulladder_1_s[0]), .Co(userfulladder_1_co));
  and and_17 (NegativeSign, SubtractionBit, userfulladder_1_s[7]);
  UserFullAdder userfulladder_2 (
    .A(and_10_out), .B(xor_2_out), .Ci(userfulladder_1_co), .S(userfulladder_1_s[1]), .Co(userfulladder_2_co));
  UserFullAdder userfulladder_3 (
    .A(and_11_out), .B(xor_3_out), .Ci(userfulladder_2_co), .S(userfulladder_1_s[2]), .Co(userfulladder_3_co));
  UserFullAdder userfulladder_4 (
    .A(and_12_out), .B(xor_4_out), .Ci(userfulladder_3_co), .S(userfulladder_1_s[3]), .Co(userfulladder_4_co));
  Multiplexer #(.width(8)) multiplexer_1 (
    .in0(userfulladder_1_s), .in1(user2scomp_1_out_2),
    .out({MSB, out_22, out_23, out_24, out_25, out_26, out_27, LSB}), .sel(NegativeSign));
  User2sComp user2scomp_1 (.in_1(userfulladder_1_s), .out_2(user2scomp_1_out_2));
  UserFullAdder userfulladder_5 (
    .A(and_13_out), .B(xor_5_out), .Ci(userfulladder_4_co), .S(userfulladder_1_s[4]), .Co(userfulladder_5_co));
  UserFullAdder userfulladder_6 (
    .A(and_14_out), .B(xor_6_out), .Ci(userfulladder_5_co), .S(userfulladder_1_s[5]), .Co(userfulladder_6_co));
  UserFullAdder userfulladder_7 (
    .A(and_15_out), .B(xor_7_out), .Ci(userfulladder_6_co), .S(userfulladder_1_s[6]), .Co(userfulladder_7_co));
  UserFullAdder userfulladder_8 (
    .A(and_16_out), .B(xor_8_out), .Ci(userfulladder_7_co), .S(userfulladder_1_s[7]), .Co(neglect));
endmodule

// HA
module UserMultiplier (
  input  A7,
  input  A6,
  input  A5,
  input  A4,
  input  A3,
  input  A2,
  input  A1,
  input  Ao,
  input  Enable,
  input  B7,
  input  B6,
  input  B5,
  input  B4,
  input  B3,
  input  B2,
  input  B1,
  input  Bo,
  output MSB,
  output out_19,
  output out_20,
  output out_21,
  output out_22,
  output out_23,
  output out_24,
  output out_25,
  output out_26,
  output out_27,
  output out_28,
  output out_29,
  output out_30,
  output out_31,
  output out_32,
  output LSB
);

  wire and_1_out, and_2_out, and_3_out, and_4_out, and_5_out, and_6_out, and_7_out, and_8_out, and_9_out,
       and_10_out, and_11_out, and_12_out, and_13_out, and_14_out, and_15_out, and_16_out, and_17_out,
       and_18_out, and_19_out, and_20_out, and_21_out, and_22_out, and_23_out, and_24_out, and_25_out,
       and_26_out, and_27_out, and_28_out, and_29_out, and_30_out, and_31_out, and_32_out, and_33_out,
       and_34_out, and_35_out, and_36_out, and_37_out, and_38_out, and_39_out, and_40_out, and_41_out,
       and_42_out, and_43_out, and_44_out, and_45_out, and_46_out, and_47_out, and_48_out, and_49_out,
       and_50_out, and_51_out, and_52_out, and_53_out, and_54_out, and_55_out, and_56_out, and_57_out,
       and_58_out, and_59_out, and_60_out, and_61_out, and_62_out, and_63_out, and_64_out, and_65_out,
       and_66_out, and_67_out, and_68_out, and_69_out, and_70_out, and_71_out, and_72_out, and_73_out,
       and_75_out, and_76_out, and_77_out, and_78_out, and_79_out, and_80_out, userfulladder_2_co,
       userfulladder_3_co, userfulladder_3_s, userfulladder_4_co, userfulladder_5_co, userfulladder_5_s,
       userfulladder_6_co, userfulladder_6_s, userfulladder_7_co, userfulladder_7_s, userfulladder_8_co,
       userfulladder_9_co, userfulladder_9_s, userfulladder_10_co, userfulladder_10_s, userfulladder_11_co,
       userfulladder_11_s, userfulladder_12_co, userfulladder_13_co, userfulladder_13_s, userfulladder_14_co,
       userfulladder_14_s, userfulladder_15_co, userfulladder_15_s, userfulladder_16_co, userfulladder_17_co,
       userfulladder_17_s, userfulladder_18_co, userfulladder_18_s, userfulladder_19_co, userfulladder_19_s,
       userfulladder_20_co, userfulladder_20_s, userfulladder_21_co, userfulladder_22_co, userfulladder_22_s,
       userfulladder_23_co, userfulladder_23_s, userfulladder_24_co, userfulladder_24_s, userfulladder_25_co,
       userfulladder_25_s, userfulladder_26_co, userfulladder_26_s, userfulladder_27_co, userfulladder_27_s,
       userfulladder_28_co, userfulladder_28_s, userfulladder_29_co, userfulladder_29_s, userfulladder_30_co,
       userfulladder_30_s, userfulladder_31_co, userfulladder_31_s, userfulladder_32_co, userfulladder_32_s,
       userfulladder_33_co, userfulladder_33_s, userfulladder_34_co, userfulladder_34_s, userfulladder_35_co,
       userfulladder_35_s, userfulladder_36_co, userfulladder_36_s, userfulladder_37_co, userfulladder_37_s,
       userfulladder_38_co, userfulladder_38_s, userfulladder_39_co, userfulladder_39_s, userfulladder_40_co,
       userfulladder_40_s, userfulladder_41_co, userfulladder_41_s, userfulladder_42_co, userfulladder_42_s,
       userfulladder_43_co, userfulladder_43_s, userfulladder_44_co, userfulladder_44_s, userfulladder_45_co,
       userfulladder_45_s, userfulladder_46_co, userfulladder_46_s, userfulladder_47_co, userfulladder_47_s,
       userfulladder_48_co, userfulladder_48_s, userhalfadder_1_c, userhalfadder_2_c, userhalfadder_2_s,
       userhalfadder_3_c, userhalfadder_4_c, userhalfadder_5_c, userhalfadder_6_c, userhalfadder_7_c,
       userhalfadder_8_c;

  and and_1 (and_1_out, and_72_out, and_59_out);
  UserFullAdder userfulladder_1 (.A(userfulladder_3_co), .B(and_1_out), .Ci(userfulladder_2_co), .S(out_19), .Co(MSB));
  and and_2 (and_2_out, and_72_out, and_60_out);
  UserFullAdder userfulladder_2 (
    .A(userfulladder_3_s), .B(and_2_out), .Ci(userfulladder_4_co), .S(out_20), .Co(userfulladder_2_co));
  and and_3 (and_3_out, and_73_out, and_59_out);
  UserFullAdder userfulladder_3 (
    .A(userfulladder_6_co), .B(and_3_out), .Ci(userfulladder_5_co), .S(userfulladder_3_s),
    .Co(userfulladder_3_co));
  UserFullAdder userfulladder_4 (
    .A(userfulladder_5_s), .B(and_5_out), .Ci(userfulladder_8_co), .S(out_21), .Co(userfulladder_4_co));
  and and_4 (and_4_out, and_73_out, and_60_out);
  UserFullAdder userfulladder_5 (
    .A(userfulladder_6_s), .B(and_4_out), .Ci(userfulladder_7_co), .S(userfulladder_5_s),
    .Co(userfulladder_5_co));
  and and_5 (and_5_out, and_72_out, and_64_out);
  and and_6 (and_6_out, and_75_out, and_59_out);
  UserFullAdder userfulladder_6 (
    .A(userfulladder_9_co), .B(and_6_out), .Ci(userfulladder_10_co), .S(userfulladder_6_s),
    .Co(userfulladder_6_co));
  and and_7 (and_7_out, and_73_out, and_64_out);
  UserFullAdder userfulladder_7 (
    .A(userfulladder_10_s), .B(and_7_out), .Ci(userfulladder_11_co), .S(userfulladder_7_s),
    .Co(userfulladder_7_co));
  and and_8 (and_8_out, and_72_out, and_65_out);
  UserFullAdder userfulladder_8 (
    .A(userfulladder_7_s), .B(and_8_out), .Ci(userfulladder_12_co), .S(out_22), .Co(userfulladder_8_co));
  and and_9 (and_9_out, and_76_out, and_59_out);
  UserFullAdder userfulladder_9 (
    .A(userfulladder_17_co), .B(and_9_out), .Ci(userfulladder_13_co), .S(userfulladder_9_s),
    .Co(userfulladder_9_co));
  and and_10 (and_10_out, and_75_out, and_60_out);
  UserFullAdder userfulladder_10 (
    .A(userfulladder_9_s), .B(and_10_out), .Ci(userfulladder_14_co), .S(userfulladder_10_s),
    .Co(userfulladder_10_co));
  and and_11 (and_11_out, and_73_out, and_65_out);
  UserFullAdder userfulladder_11 (
    .A(userfulladder_14_s), .B(and_11_out), .Ci(userfulladder_15_co), .S(userfulladder_11_s),
    .Co(userfulladder_11_co));
  and and_12 (and_12_out, and_72_out, and_66_out);
  UserFullAdder userfulladder_12 (
    .A(userfulladder_11_s), .B(and_12_out), .Ci(userfulladder_16_co), .S(out_23), .Co(userfulladder_12_co));
  and and_13 (and_13_out, and_76_out, and_60_out);
  UserFullAdder userfulladder_13 (
    .A(userfulladder_17_s), .B(and_13_out), .Ci(userfulladder_18_co), .S(userfulladder_13_s),
    .Co(userfulladder_13_co));
  and and_14 (and_14_out, and_75_out, and_64_out);
  UserFullAdder userfulladder_14 (
    .A(userfulladder_13_s), .B(and_14_out), .Ci(userfulladder_19_co), .S(userfulladder_14_s),
    .Co(userfulladder_14_co));
  and and_15 (and_15_out, and_73_out, and_66_out);
  UserFullAdder userfulladder_15 (
    .A(userfulladder_19_s), .B(and_15_out), .Ci(userfulladder_20_co), .S(userfulladder_15_s),
    .Co(userfulladder_15_co));
  and and_16 (and_16_out, and_72_out, and_68_out);
  UserFullAdder userfulladder_16 (
    .A(userfulladder_15_s), .B(and_16_out), .Ci(userfulladder_21_co), .S(out_24), .Co(userfulladder_16_co));
  and and_17 (and_17_out, and_77_out, and_59_out);
  UserFullAdder userfulladder_17 (
    .A(userfulladder_22_co), .B(and_17_out), .Ci(userfulladder_23_co), .S(userfulladder_17_s),
    .Co(userfulladder_17_co));
  and and_18 (and_18_out, and_76_out, and_64_out);
  UserFullAdder userfulladder_18 (
    .A(userfulladder_23_s), .B(and_18_out), .Ci(userfulladder_24_co), .S(userfulladder_18_s),
    .Co(userfulladder_18_co));
  and and_19 (and_19_out, and_75_out, and_65_out);
  UserFullAdder userfulladder_19 (
    .A(userfulladder_18_s), .B(and_19_out), .Ci(userfulladder_25_co), .S(userfulladder_19_s),
    .Co(userfulladder_19_co));
  UserFullAdder userfulladder_20 (
    .A(userfulladder_25_s), .B(and_23_out), .Ci(userfulladder_29_co), .S(userfulladder_20_s),
    .Co(userfulladder_20_co));
  and and_20 (and_20_out, and_72_out, and_69_out);
  UserFullAdder userfulladder_21 (
    .A(userfulladder_20_s), .B(and_20_out), .Ci(userhalfadder_1_c), .S(out_25), .Co(userfulladder_21_co));
  UserFullAdder userfulladder_22 (
    .A(userhalfadder_2_c), .B(and_25_out), .Ci(userfulladder_26_co), .S(userfulladder_22_s),
    .Co(userfulladder_22_co));
  and and_21 (and_21_out, and_77_out, and_60_out);
  UserFullAdder userfulladder_23 (
    .A(userfulladder_22_s), .B(and_21_out), .Ci(userfulladder_27_co), .S(userfulladder_23_s),
    .Co(userfulladder_23_co));
  UserFullAdder userfulladder_24 (
    .A(userfulladder_27_s), .B(and_27_out), .Ci(userfulladder_31_co), .S(userfulladder_24_s),
    .Co(userfulladder_24_co));
  and and_22 (and_22_out, and_75_out, and_66_out);
  UserFullAdder userfulladder_25 (
    .A(userfulladder_24_s), .B(and_22_out), .Ci(userfulladder_28_co), .S(userfulladder_25_s),
    .Co(userfulladder_25_co));
  and and_23 (and_23_out, and_73_out, and_68_out);
  and and_24 (and_24_out, and_72_out, and_70_out);
  UserHalfAdder userhalfadder_1 (.A(userfulladder_29_s), .B(and_24_out), .S(out_26), .C(userhalfadder_1_c));
  and and_25 (and_25_out, and_78_out, and_59_out);
  UserFullAdder userfulladder_26 (
    .A(userhalfadder_2_s), .B(and_31_out), .Ci(userfulladder_34_co), .S(userfulladder_26_s),
    .Co(userfulladder_26_co));
  and and_26 (and_26_out, and_77_out, and_64_out);
  UserFullAdder userfulladder_27 (
    .A(userfulladder_26_s), .B(and_26_out), .Ci(userfulladder_30_co), .S(userfulladder_27_s),
    .Co(userfulladder_27_co));
  and and_27 (and_27_out, and_76_out, and_65_out);
  and and_28 (and_28_out, and_75_out, and_68_out);
  UserFullAdder userfulladder_28 (
    .A(userfulladder_31_s), .B(and_28_out), .Ci(userfulladder_32_co), .S(userfulladder_28_s),
    .Co(userfulladder_28_co));
  and and_29 (and_29_out, and_73_out, and_69_out);
  UserFullAdder userfulladder_29 (
    .A(userfulladder_28_s), .B(and_29_out), .Ci(userhalfadder_3_c), .S(userfulladder_29_s),
    .Co(userfulladder_29_co));
  and and_30 (and_30_out, and_79_out, and_59_out);
  UserHalfAdder userhalfadder_2 (.A(userfulladder_33_co), .B(and_30_out), .S(userhalfadder_2_s), .C(userhalfadder_2_c));
  and and_31 (and_31_out, and_78_out, and_60_out);
  and and_32 (and_32_out, and_77_out, and_65_out);
  UserFullAdder userfulladder_30 (
    .A(userfulladder_34_s), .B(and_32_out), .Ci(userfulladder_35_co), .S(userfulladder_30_s),
    .Co(userfulladder_30_co));
  and and_33 (and_33_out, and_76_out, and_66_out);
  UserFullAdder userfulladder_31 (
    .A(userfulladder_30_s), .B(and_33_out), .Ci(userfulladder_36_co), .S(userfulladder_31_s),
    .Co(userfulladder_31_co));
  and and_34 (and_34_out, and_75_out, and_69_out);
  UserFullAdder userfulladder_32 (
    .A(userfulladder_36_s), .B(and_34_out), .Ci(userhalfadder_4_c), .S(userfulladder_32_s),
    .Co(userfulladder_32_co));
  and and_35 (and_35_out, and_73_out, and_70_out);
  UserHalfAdder userhalfadder_3 (.A(userfulladder_32_s), .B(and_35_out), .S(out_27), .C(userhalfadder_3_c));
  and and_36 (and_36_out, and_79_out, and_60_out);
  UserFullAdder userfulladder_33 (
    .A(and_40_out), .B(and_36_out), .Ci(userfulladder_37_co), .S(userfulladder_33_s), .Co(userfulladder_33_co));
  and and_37 (and_37_out, and_78_out, and_64_out);
  UserFullAdder userfulladder_34 (
    .A(userfulladder_33_s), .B(and_37_out), .Ci(userfulladder_38_co), .S(userfulladder_34_s),
    .Co(userfulladder_34_co));
  and and_38 (and_38_out, and_77_out, and_66_out);
  UserFullAdder userfulladder_35 (
    .A(userfulladder_38_s), .B(and_38_out), .Ci(userfulladder_39_co), .S(userfulladder_35_s),
    .Co(userfulladder_35_co));
  and and_39 (and_39_out, and_76_out, and_68_out);
  UserFullAdder userfulladder_36 (
    .A(userfulladder_35_s), .B(and_39_out), .Ci(userfulladder_40_co), .S(userfulladder_36_s),
    .Co(userfulladder_36_co));
  and and_40 (and_40_out, and_59_out, and_80_out);
  and and_41 (and_41_out, and_79_out, and_64_out);
  UserFullAdder userfulladder_37 (
    .A(and_46_out), .B(and_41_out), .Ci(userfulladder_41_co), .S(userfulladder_37_s), .Co(userfulladder_37_co));
  and and_42 (and_42_out, and_78_out, and_65_out);
  UserFullAdder userfulladder_38 (
    .A(userfulladder_37_s), .B(and_42_out), .Ci(userfulladder_42_co), .S(userfulladder_38_s),
    .Co(userfulladder_38_co));
  and and_43 (and_43_out, and_77_out, and_68_out);
  UserFullAdder userfulladder_39 (
    .A(userfulladder_42_s), .B(and_43_out), .Ci(userfulladder_43_co), .S(userfulladder_39_s),
    .Co(userfulladder_39_co));
  and and_44 (and_44_out, and_76_out, and_69_out);
  UserFullAdder userfulladder_40 (
    .A(userfulladder_39_s), .B(and_44_out), .Ci(userhalfadder_5_c), .S(userfulladder_40_s),
    .Co(userfulladder_40_co));
  and and_45 (and_45_out, and_75_out, and_70_out);
  UserHalfAdder userhalfadder_4 (.A(userfulladder_40_s), .B(and_45_out), .S(out_28), .C(userhalfadder_4_c));
  and and_46 (and_46_out, and_60_out, and_80_out);
  and and_47 (and_47_out, and_79_out, and_65_out);
  UserFullAdder userfulladder_41 (
    .A(and_50_out), .B(and_47_out), .Ci(userfulladder_44_co), .S(userfulladder_41_s), .Co(userfulladder_41_co));
  and and_48 (and_48_out, and_78_out, and_66_out);
  UserFullAdder userfulladder_42 (
    .A(userfulladder_41_s), .B(and_48_out), .Ci(userfulladder_45_co), .S(userfulladder_42_s),
    .Co(userfulladder_42_co));
  UserFullAdder userfulladder_43 (
    .A(userfulladder_45_s), .B(and_52_out), .Ci(userhalfadder_6_c), .S(userfulladder_43_s),
    .Co(userfulladder_43_co));
  and and_49 (and_49_out, and_76_out, and_70_out);
  UserHalfAdder userhalfadder_5 (.A(userfulladder_43_s), .B(and_49_out), .S(out_29), .C(userhalfadder_5_c));
  and and_50 (and_50_out, and_64_out, and_80_out);
  UserFullAdder userfulladder_44 (
    .A(and_53_out), .B(and_54_out), .Ci(userfulladder_47_co), .S(userfulladder_44_s), .Co(userfulladder_44_co));
  and and_51 (and_51_out, and_78_out, and_68_out);
  UserFullAdder userfulladder_45 (
    .A(userfulladder_44_s), .B(and_51_out), .Ci(userfulladder_46_co), .S(userfulladder_45_s),
    .Co(userfulladder_45_co));
  and and_52 (and_52_out, and_77_out, and_69_out);
  and and_53 (and_53_out, and_65_out, and_80_out);
  and and_54 (and_54_out, and_79_out, and_66_out);
  and and_55 (and_55_out, and_78_out, and_69_out);
  UserFullAdder userfulladder_46 (
    .A(userfulladder_47_s), .B(and_55_out), .Ci(userhalfadder_7_c), .S(userfulladder_46_s),
    .Co(userfulladder_46_co));
  and and_56 (and_56_out, and_77_out, and_70_out);
  UserHalfAdder userhalfadder_6 (.A(userfulladder_46_s), .B(and_56_out), .S(out_30), .C(userhalfadder_6_c));
  and and_57 (and_57_out, and_66_out, and_80_out);
  and and_58 (and_58_out, and_79_out, and_68_out);
  UserFullAdder userfulladder_47 (
    .A(and_57_out), .B(and_58_out), .Ci(userfulladder_48_co), .S(userfulladder_47_s), .Co(userfulladder_47_co));
  and and_59 (and_59_out, Enable, A7);
  and and_60 (and_60_out, Enable, A6);
  and and_61 (and_61_out, and_68_out, and_80_out);
  and and_62 (and_62_out, and_79_out, and_69_out);
  UserFullAdder userfulladder_48 (
    .A(and_61_out), .B(and_62_out), .Ci(userhalfadder_8_c), .S(userfulladder_48_s), .Co(userfulladder_48_co));
  and and_63 (and_63_out, and_78_out, and_70_out);
  UserHalfAdder userhalfadder_7 (.A(userfulladder_48_s), .B(and_63_out), .S(out_31), .C(userhalfadder_7_c));
  and and_64 (and_64_out, Enable, A5);
  and and_65 (and_65_out, Enable, A4);
  and and_66 (and_66_out, Enable, A3);
  and and_67 (and_67_out, and_79_out, and_70_out);
  UserHalfAdder userhalfadder_8 (.A(and_71_out), .B(and_67_out), .S(out_32), .C(userhalfadder_8_c));
  and and_68 (and_68_out, Enable, A2);
  and and_69 (and_69_out, Enable, A1);
  and and_70 (and_70_out, Enable, Ao);
  and and_71 (and_71_out, and_69_out, and_80_out);
  and and_72 (and_72_out, Enable, B7);
  and and_73 (and_73_out, Enable, B6);
  and and_74 (LSB, and_70_out, and_80_out);
  and and_75 (and_75_out, Enable, B5);
  and and_76 (and_76_out, Enable, B4);
  and and_77 (and_77_out, Enable, B3);
  and and_78 (and_78_out, Enable, B2);
  and and_79 (and_79_out, Enable, B1);
  and and_80 (and_80_out, Enable, Bo);
endmodule

module UserDivider (
  input  E,
  input  A7,
  input  A6,
  input  A5,
  input  A4,
  input  A3,
  input  A2,
  input  A1,
  input  Ao,
  input  B7,
  input  B6,
  input  B5,
  input  B4,
  input  B3,
  input  B2,
  input  B1,
  input  Bo,
  output LSB,
  output out_19,
  output out_20,
  output out_21,
  output out_22,
  output out_23,
  output out_24,
  output MSB
);

  wire [7:0] and_1_out, and_2_out;

  assign and_1_out = {A7, A6, A5, A4, A3, A2, A1, Ao} & {8{E}};  // AND_Gate and_1, 8 bits wide
  Divider divider_1 (
    .a(and_1_out), .b(and_2_out), .out({MSB, out_24, out_23, out_22, out_21, out_20, out_19, LSB}));  // open: upper, rem
  assign and_2_out = {B7, B6, B5, B4, B3, B2, B1, Bo} & {8{E}};  // AND_Gate and_2, 8 bits wide
endmodule

module UserBCDto7Seg (
  input  D3,
  input  D2,
  input  D1,
  input  Do,
  output g,
  output f,
  output e,
  output d,
  output c,
  output b,
  output a
);

  wire and_1_out, and_2_out, and_3_out, and_4_out, and_5_out, and_6_out, and_7_out, and_8_out, and_9_out,
       and_10_out, and_11_out, and_12_out, and_13_out, and_14_out, not_1_out, not_2_out, not_3_out, not_4_out;

  not not_1 (not_1_out, D3);
  not not_2 (not_2_out, D2);
  not not_3 (not_3_out, D1);
  not not_4 (not_4_out, Do);
  and and_1 (and_1_out, not_1_out, not_2_out, not_3_out);
  and and_2 (and_2_out, not_1_out, D2, D1, Do);
  and and_3 (and_3_out, not_1_out, not_2_out, D1);
  and and_4 (and_4_out, not_1_out, not_2_out, Do);
  and and_5 (and_5_out, not_1_out, D1, Do);
  and and_6 (and_6_out, not_1_out, D1, not_4_out);
  and and_7 (and_7_out, not_2_out, not_3_out, not_4_out);
  and and_8 (and_8_out, not_1_out, not_2_out, not_3_out, Do);
  and and_9 (and_9_out, not_1_out, D2, not_3_out, not_4_out);
  and and_10 (and_10_out, not_1_out, D2, D1, Do);
  nand nand_1 (c, not_1_out, not_2_out, D1, not_4_out);
  and and_11 (and_11_out, not_1_out, D2, not_3_out, Do);
  and and_12 (and_12_out, not_1_out, D2, D1, not_4_out);
  and and_13 (and_13_out, not_1_out, not_2_out, not_3_out, Do);
  and and_14 (and_14_out, not_1_out, D2, not_3_out, not_4_out);
  nor nor_1 (g, and_1_out, and_2_out);
  nor nor_2 (f, and_3_out, and_4_out, and_5_out);
  or or_1 (e, and_6_out, and_7_out);
  nor nor_3 (d, and_8_out, and_9_out, and_10_out);
  nor nor_4 (b, and_11_out, and_12_out);
  nor nor_5 (a, and_13_out, and_14_out);
endmodule

module UserDecoder_2x4 (
  input  i1,
  input  i0,
  input  EN,
  output o3,
  output o2,
  output o1,
  output o0
);

  wire and_1_out, and_2_out, and_3_out, and_4_out;

  and and_1 (and_1_out, i1, i0);
  and and_2 (and_2_out, i1, ~i0);  // AND_Gate
  and and_3 (and_3_out, ~i1, i0);  // AND_Gate
  and and_4 (and_4_out, ~i1, ~i0);  // AND_Gate
  and and_5 (o3, EN, and_1_out);
  and and_6 (o2, EN, and_2_out);
  and and_7 (o1, EN, and_3_out);
  and and_8 (o0, EN, and_4_out);
endmodule

module UserControlUnit (
  input  rc_2,
  input  rc_1,
  input  rc_0,
  input  CLK,
  output rc_2_2,
  output rc_2_1,
  output rc_2_0,
  output rc_1_4,
  output rc_1_3,
  output rc_1_2,
  output rc_1_1,
  output rc_1_0,
  output rc_0_3,
  output rc_0_2,
  output rc_0_1,
  output rc_0_0
);

  UserRingCounter3 userringcounter3_1 (.PULSE(rc_2), .CLK(CLK), .o2(rc_2_2), .o1(rc_2_1), .o0(rc_2_0));
  UserRingCounter5 userringcounter5_1 (
    .PULSE(rc_1), .CLK(CLK), .o4(rc_1_4), .o3(rc_1_3), .o2(rc_1_2), .o1(rc_1_1), .o0(rc_1_0));
  UserRingCounter4 userringcounter4_1 (.PULSE(rc_0), .CLK(CLK), .o3(rc_0_3), .o2(rc_0_2), .o1(rc_0_1), .o0(rc_0_0));
endmodule

module UserEncoder_4x2 (
  input  i3,
  input  i2,
  input  i1,
  input  i0,
  output o1,
  output o0
);

  or or_1 (o1, i3, i2);
  or or_2 (o0, i3, i1);
endmodule

module UserJKFlipFlop (
  input  J,
  input  K,
  input  CLK,
  input  CLR,
  output out_5,
  output out_6
);

  wire and_1_out, and_2_out, nand_1_out, nand_2_out, nand_3_out, nand_4_out, nand_5_out, nand_6_out,
       not_1_out, not_2_out, or_1_out, or_2_out;

  or or_1 (or_1_out, CLK, CLR);
  or or_2 (or_2_out, K, CLR);
  nand nand_1 (nand_1_out, J, out_6, or_1_out);
  nand nand_2 (nand_2_out, or_1_out, out_5, or_2_out);
  nand nand_3 (nand_3_out, nand_1_out, nand_4_out);
  nand nand_4 (nand_4_out, nand_3_out, nand_2_out);
  not not_1 (not_1_out, CLR);
  not not_2 (not_2_out, or_1_out);
  nand nand_5 (nand_5_out, nand_3_out, not_2_out);
  nand nand_6 (nand_6_out, not_2_out, nand_4_out);
  and and_1 (and_1_out, nand_5_out, not_1_out);
  and and_2 (and_2_out, nand_6_out, not_1_out);
  nand nand_7 (out_5, and_1_out, out_6);
  nand nand_8 (out_6, out_5, and_2_out);
endmodule

module UserRingCounter3 (
  input  PULSE,
  input  CLK,
  output o2,
  output o1,
  output o0
);

  wire d_ff_1_q, d_ff_5_q, j_k_ff_1_q, or_1_out, or_2_out;

  or or_1 (or_1_out, PULSE, d_ff_5_q);
  J_K_Flip_Flop j_k_ff_1 (.J(1'b1), .K(1'b1), .clk(or_1_out), .Q(j_k_ff_1_q));  // open: Qn, preset, reset
  D_Flip_Flop d_ff_1 (.D(d_ff_5_q), .clk(CLK), .Q(d_ff_1_q), .preset(or_1_out), .reset(j_k_ff_1_q));  // open: Qn
  or or_2 (or_2_out, j_k_ff_1_q, or_1_out);
  D_Flip_Flop d_ff_2 (.D(d_ff_1_q), .clk(CLK), .Q(o0), .reset(or_2_out));  // open: Qn, preset
  D_Flip_Flop d_ff_3 (.D(o0), .clk(CLK), .Q(o1), .reset(or_2_out));  // open: Qn, preset
  D_Flip_Flop d_ff_4 (.D(o1), .clk(CLK), .Q(o2), .reset(or_2_out));  // open: Qn, preset
  D_Flip_Flop d_ff_5 (.D(o2), .clk(CLK), .Q(d_ff_5_q), .reset(or_2_out));  // open: Qn, preset
  // AND_Gate and_1 is placed but not wired
endmodule

module UserRingCounter5 (
  input  PULSE,
  input  CLK,
  output o4,
  output o3,
  output o2,
  output o1,
  output o0
);

  wire d_ff_1_q, d_ff_7_q, j_k_ff_1_q, or_1_out, or_2_out;

  or or_1 (or_1_out, PULSE, d_ff_7_q);
  J_K_Flip_Flop j_k_ff_1 (.J(1'b1), .K(1'b1), .clk(or_1_out), .Q(j_k_ff_1_q));  // open: Qn, preset, reset
  D_Flip_Flop d_ff_1 (.D(d_ff_7_q), .clk(CLK), .Q(d_ff_1_q), .preset(or_1_out), .reset(j_k_ff_1_q));  // open: Qn
  or or_2 (or_2_out, j_k_ff_1_q, or_1_out);
  D_Flip_Flop d_ff_2 (.D(d_ff_1_q), .clk(CLK), .Q(o0), .reset(or_2_out));  // open: Qn, preset
  D_Flip_Flop d_ff_3 (.D(o0), .clk(CLK), .Q(o1), .reset(or_2_out));  // open: Qn, preset
  D_Flip_Flop d_ff_4 (.D(o1), .clk(CLK), .Q(o2), .reset(or_2_out));  // open: Qn, preset
  D_Flip_Flop d_ff_5 (.D(o2), .clk(CLK), .Q(o3), .reset(or_2_out));  // open: Qn, preset
  D_Flip_Flop d_ff_6 (.D(o3), .clk(CLK), .Q(o4), .reset(or_2_out));  // open: Qn, preset
  D_Flip_Flop d_ff_7 (.D(o4), .clk(CLK), .Q(d_ff_7_q));  // open: Qn, preset, reset
endmodule

module Board (
  input  in_1,
  input  in_2,
  input  in_3,
  input  in_4
);

  wire alu_1_neg, alu_1_overflow, userbcdto7seg_1_p1, userbcdto7seg_1_p2, userbcdto7seg_1_p3,
       userbcdto7seg_1_p5, userbcdto7seg_1_p7, userbcdto7seg_1_p9, userbcdto7seg_1_p12, userbcdto7seg_1_p13,
       userbcdto7seg_1_p15, userbcdto7seg_1_p16, userbcdto7seg_1_p18, userbcdto7seg_1_p20,
       userbcdto7seg_1_p22, userbcdto7seg_2_p15, userbcdto7seg_2_p17, userbcdto7seg_2_p18,
       userbcdto7seg_2_p19, userbcdto7seg_2_p21, userbcdto7seg_2_p23, userbcdto7seg_2_p26,
       userbcdto7seg_3_p15;
  wire [3:0] userbcdto7seg_1_p10, userbcdto7seg_1_p23, userbcdto7seg_2_p25;
  wire [7:0] dipswitch_1_sw8, dipswitch_2_sw8, userbcdto7seg_1_p11;

  DipSwitch dipswitch_1 (
    .sw1(dipswitch_1_sw8[7]), .sw2(dipswitch_1_sw8[6]), .sw3(dipswitch_1_sw8[5]), .sw4(dipswitch_1_sw8[4]),
    .sw5(dipswitch_1_sw8[3]), .sw6(dipswitch_1_sw8[2]), .sw7(dipswitch_1_sw8[1]), .sw8(dipswitch_1_sw8[0]));
  DipSwitch dipswitch_2 (
    .sw1(dipswitch_2_sw8[7]), .sw2(dipswitch_2_sw8[6]), .sw3(dipswitch_2_sw8[5]), .sw4(dipswitch_2_sw8[4]),
    .sw5(dipswitch_2_sw8[3]), .sw6(dipswitch_2_sw8[2]), .sw7(dipswitch_2_sw8[1]), .sw8(dipswitch_2_sw8[0]));
  LED led_1 (.in(alu_1_overflow));
  _7_Segment_Display u_7_segment_display_1 (.g(alu_1_neg));  // open: f, a, b, e, d, c, dp
  // UserBCDto7Seg userbcdto7seg_1: pin names not known; wires that end beside it: userbcdto7seg_1_p1, userbcdto7seg_1_p2, userbcdto7seg_1_p3, userbcdto7seg_1_p10[3], userbcdto7seg_1_p5, userbcdto7seg_1_p10[2], userbcdto7seg_1_p7, userbcdto7seg_1_p10[1], userbcdto7seg_1_p9, userbcdto7seg_1_p10[0], userbcdto7seg_1_p11, userbcdto7seg_1_p12, userbcdto7seg_1_p13, userbcdto7seg_1_p10, userbcdto7seg_1_p15, userbcdto7seg_1_p16, userbcdto7seg_1_p23[3], userbcdto7seg_1_p18, userbcdto7seg_1_p23[2], userbcdto7seg_1_p20, userbcdto7seg_1_p23[1], userbcdto7seg_1_p22, userbcdto7seg_1_p23[0], userbcdto7seg_1_p23
  ALU alu_1 (
    .A7(dipswitch_1_sw8[7]), .A6(dipswitch_1_sw8[6]), .A5(dipswitch_1_sw8[5]), .A4(dipswitch_1_sw8[4]),
    .A3(dipswitch_1_sw8[3]), .A2(dipswitch_1_sw8[2]), .A1(dipswitch_1_sw8[1]), .Ao(dipswitch_1_sw8[0]),
    .B7(dipswitch_2_sw8[7]), .B6(dipswitch_2_sw8[6]), .B5(dipswitch_2_sw8[5]), .B4(dipswitch_2_sw8[4]),
    .B3(dipswitch_2_sw8[3]), .B2(dipswitch_2_sw8[2]), .B1(dipswitch_2_sw8[1]), .Bo(dipswitch_2_sw8[0]),
    .ADD(in_1), .SUB(in_2), .MUL(in_3), .DIV(in_4), .neg(alu_1_neg), .MSB(userbcdto7seg_1_p11[7]),
    .out_24(userbcdto7seg_1_p11[6]), .out_25(userbcdto7seg_1_p11[5]), .out_26(userbcdto7seg_1_p11[4]),
    .out_27(userbcdto7seg_1_p11[3]), .out_28(userbcdto7seg_1_p11[2]), .out_29(userbcdto7seg_1_p11[1]),
    .LSB(userbcdto7seg_1_p11[0]), .OVERFLOW(alu_1_overflow));
  _7_Segment_Display u_7_segment_display_2 (
    .g(userbcdto7seg_1_p1), .f(userbcdto7seg_1_p2), .a(userbcdto7seg_1_p12), .b(userbcdto7seg_1_p9),
    .e(userbcdto7seg_1_p3), .d(userbcdto7seg_1_p5), .c(userbcdto7seg_1_p7));  // open: dp
  // UserBCDto7Seg userbcdto7seg_2: pin names not known; wires that end beside it: userbcdto7seg_1_p9, userbcdto7seg_1_p10[0], userbcdto7seg_1_p11, userbcdto7seg_1_p13, userbcdto7seg_1_p10, userbcdto7seg_1_p15, userbcdto7seg_1_p16, userbcdto7seg_1_p23[3], userbcdto7seg_1_p18, userbcdto7seg_1_p23[2], userbcdto7seg_1_p20, userbcdto7seg_1_p23[1], userbcdto7seg_1_p22, userbcdto7seg_1_p23[0], userbcdto7seg_2_p15, userbcdto7seg_1_p23, userbcdto7seg_2_p17, userbcdto7seg_2_p18, userbcdto7seg_2_p19, userbcdto7seg_2_p25[3], userbcdto7seg_2_p21, userbcdto7seg_2_p25[2], userbcdto7seg_2_p23, userbcdto7seg_2_p25[1], userbcdto7seg_2_p25, userbcdto7seg_2_p26, userbcdto7seg_2_p25[0]
  // Binary_to_BCD_converter #(.binvalue(8)) binary_to_bcd_converter_1: pin names not known
  _7_Segment_Display u_7_segment_display_3 (
    .g(userbcdto7seg_1_p13), .f(userbcdto7seg_1_p15), .a(userbcdto7seg_2_p15), .b(userbcdto7seg_1_p22),
    .e(userbcdto7seg_1_p16), .d(userbcdto7seg_1_p18), .c(userbcdto7seg_1_p20));  // open: dp
  // UserBCDto7Seg userbcdto7seg_3: pin names not known; wires that end beside it: userbcdto7seg_1_p22, userbcdto7seg_1_p23[0], userbcdto7seg_1_p23, userbcdto7seg_2_p17, userbcdto7seg_2_p18, userbcdto7seg_2_p19, userbcdto7seg_2_p25[3], userbcdto7seg_2_p21, userbcdto7seg_2_p25[2], userbcdto7seg_2_p23, userbcdto7seg_2_p25[1], userbcdto7seg_2_p25, userbcdto7seg_2_p26, userbcdto7seg_2_p25[0], userbcdto7seg_3_p15
  _7_Segment_Display u_7_segment_display_4 (
    .g(userbcdto7seg_2_p17), .f(userbcdto7seg_2_p18), .a(userbcdto7seg_3_p15), .b(userbcdto7seg_2_p26),
    .e(userbcdto7seg_2_p19), .d(userbcdto7seg_2_p21), .c(userbcdto7seg_2_p23));  // open: dp
endmodule

module ALU (
  input  ADD,
  input  SUB,
  input  MUL,
  input  DIV,
  input  A7,
  input  A6,
  input  A5,
  input  A4,
  input  A3,
  input  A2,
  input  A1,
  input  Ao,
  input  B7,
  input  B6,
  input  B5,
  input  B4,
  input  B3,
  input  B2,
  input  B1,
  input  Bo,
  output OVERFLOW,
  output neg,
  output MSB,
  output out_24,
  output out_25,
  output out_26,
  output out_27,
  output out_28,
  output out_29,
  output LSB
);

  wire or_1_out, useraddandsub_1_lsb, useraddandsub_1_msb, useraddandsub_1_neglect, useraddandsub_1_out_22,
       useraddandsub_1_out_23, useraddandsub_1_out_24, useraddandsub_1_out_25, useraddandsub_1_out_26,
       useraddandsub_1_out_27, userdivider_1_lsb, userdivider_1_msb, userdivider_1_out_19,
       userdivider_1_out_20, userdivider_1_out_21, userdivider_1_out_22, userdivider_1_out_23,
       userdivider_1_out_24, usermultiplier_1_lsb, usermultiplier_1_msb, usermultiplier_1_out_19,
       usermultiplier_1_out_20, usermultiplier_1_out_21, usermultiplier_1_out_22, usermultiplier_1_out_23,
       usermultiplier_1_out_24, usermultiplier_1_out_25, usermultiplier_1_out_26, usermultiplier_1_out_27,
       usermultiplier_1_out_28, usermultiplier_1_out_29, usermultiplier_1_out_30, usermultiplier_1_out_31,
       usermultiplier_1_out_32;

  or or_1 (or_1_out, ADD, SUB);
  UserAddAndSub useraddandsub_1 (
    .SubtractionBit(SUB), .Enable(or_1_out), .Bo(Bo), .B1(B1), .B2(B2), .B3(B3), .B4(B4), .B5(B5), .B6(B6),
    .B7(B7), .Ao(Ao), .A1(A1), .A2(A2), .A3(A3), .A4(A4), .A5(A5), .A6(A6), .A7(A7),
    .LSB(useraddandsub_1_lsb), .neglect(useraddandsub_1_neglect), .NegativeSign(neg),
    .MSB(useraddandsub_1_msb), .out_22(useraddandsub_1_out_22), .out_23(useraddandsub_1_out_23),
    .out_24(useraddandsub_1_out_24), .out_25(useraddandsub_1_out_25), .out_26(useraddandsub_1_out_26),
    .out_27(useraddandsub_1_out_27));
  UserDivider userdivider_1 (
    .E(DIV), .A7(A7), .A6(A6), .A5(A5), .A4(A4), .A3(A3), .A2(A2), .A1(A1), .Ao(Ao), .B7(B7), .B6(B6),
    .B5(B5), .B4(B4), .B3(B3), .B2(B2), .B1(B1), .Bo(Bo), .LSB(userdivider_1_lsb),
    .out_19(userdivider_1_out_19), .out_20(userdivider_1_out_20), .out_21(userdivider_1_out_21),
    .out_22(userdivider_1_out_22), .out_23(userdivider_1_out_23), .out_24(userdivider_1_out_24),
    .MSB(userdivider_1_msb));
  or or_2 (OVERFLOW, useraddandsub_1_neglect, usermultiplier_1_msb, usermultiplier_1_out_19, usermultiplier_1_out_20, usermultiplier_1_out_21, usermultiplier_1_out_22, usermultiplier_1_out_23, usermultiplier_1_out_24, usermultiplier_1_out_25);
  UserMultiplier usermultiplier_1 (
    .Enable(MUL), .A7(A7), .A6(A6), .A5(A5), .A4(A4), .A3(A3), .A2(A2), .A1(A1), .Ao(Ao), .B7(B7), .B6(B6),
    .B5(B5), .B4(B4), .B3(B3), .B2(B2), .B1(B1), .Bo(Bo), .MSB(usermultiplier_1_msb),
    .out_19(usermultiplier_1_out_19), .out_20(usermultiplier_1_out_20), .out_21(usermultiplier_1_out_21),
    .out_22(usermultiplier_1_out_22), .out_23(usermultiplier_1_out_23), .out_24(usermultiplier_1_out_24),
    .out_25(usermultiplier_1_out_25), .out_26(usermultiplier_1_out_26), .out_27(usermultiplier_1_out_27),
    .out_28(usermultiplier_1_out_28), .out_29(usermultiplier_1_out_29), .out_30(usermultiplier_1_out_30),
    .out_31(usermultiplier_1_out_31), .out_32(usermultiplier_1_out_32), .LSB(usermultiplier_1_lsb));
  or or_3 (MSB, useraddandsub_1_msb, usermultiplier_1_out_26, userdivider_1_msb);
  or or_4 (out_24, useraddandsub_1_out_22, usermultiplier_1_out_27, userdivider_1_out_24);
  or or_5 (out_25, useraddandsub_1_out_23, usermultiplier_1_out_28, userdivider_1_out_23);
  or or_6 (out_26, useraddandsub_1_out_24, usermultiplier_1_out_29, userdivider_1_out_22);
  or or_7 (out_27, useraddandsub_1_out_25, usermultiplier_1_out_30, userdivider_1_out_21);
  or or_8 (out_28, useraddandsub_1_out_26, usermultiplier_1_out_31, userdivider_1_out_20);
  or or_9 (out_29, useraddandsub_1_out_27, usermultiplier_1_out_32, userdivider_1_out_19);
  or or_10 (LSB, useraddandsub_1_lsb, usermultiplier_1_lsb, userdivider_1_lsb);
endmodule

module User21Mux (
  input  [7:0] Ao,
  input  [7:0] A1,
  input  [7:0] S,
  output [7:0] O
);

  wire [7:0] and_1_out, and_2_out, not_1_out;

  assign not_1_out = ~S;  // NOT_Gate not_1, 8 bits wide
  assign and_1_out = S & A1;  // AND_Gate and_1, 8 bits wide
  assign and_2_out = Ao & not_1_out;  // AND_Gate and_2, 8 bits wide
  assign O = and_1_out | and_2_out;  // OR_Gate or_1, 8 bits wide
endmodule

module User2sComp (
  input  [7:0] in_1,
  output [7:0] out_2
);

  wire [7:0] not_1_out;

  assign not_1_out = ~in_1;  // NOT_Gate not_1, 8 bits wide
  Adder adder_1 (.a(not_1_out), .b(8'h1), .out(out_2), .cin(1'b0));  // open: cout
endmodule
