// Logisim project Version_01.circ as structural Verilog: 1 circuit, main circuit main
module main (
  input  LSB,
  input  in_2,
  input  in_3,
  input  in_4,
  input  in_5,
  input  in_6,
  input  in_7,
  input  MSB,
  input  in_9,
  input  Sub_Bit,
  input  LSB_2,
  input  in_12,
  input  in_13,
  input  in_14,
  input  in_15,
  input  in_16,
  input  in_17,
  input  MSB_2
);

  wire adder_1_cout, adder_1_out, adder_2_cout, adder_2_out, adder_3_cout, adder_3_out, adder_4_cout,
       adder_4_out, adder_5_cout, adder_5_out, adder_6_cout, adder_6_out, adder_7_cout, adder_7_out,
       adder_8_cout, adder_8_out, xor_1_out, xor_2_out, xor_3_out, xor_4_out, xor_5_out, xor_6_out,
       xor_7_out, xor_8_out;

  xor xor_1 (xor_1_out, Sub_Bit, LSB_2);
  xor xor_2 (xor_2_out, Sub_Bit, in_12);
  xor xor_3 (xor_3_out, Sub_Bit, in_13);
  xor xor_4 (xor_4_out, Sub_Bit, in_14);
  xor xor_5 (xor_5_out, Sub_Bit, in_15);
  xor xor_6 (xor_6_out, Sub_Bit, in_16);
  xor xor_7 (xor_7_out, Sub_Bit, in_17);
  xor xor_8 (xor_8_out, Sub_Bit, MSB_2);
  Adder #(.width(1)) adder_1 (.a(LSB), .b(xor_1_out), .out(adder_1_out), .cin(Sub_Bit), .cout(adder_1_cout));
  Adder #(.width(1)) adder_2 (.a(in_2), .b(xor_2_out), .out(adder_2_out), .cin(adder_1_cout), .cout(adder_2_cout));
  Adder #(.width(1)) adder_3 (.a(in_4), .b(xor_3_out), .out(adder_3_out), .cin(adder_2_cout), .cout(adder_3_cout));
  // Probe on adder_1_out
  // Probe on adder_2_out
  // Probe on adder_2_out
  Adder #(.width(1)) adder_4 (.a(in_5), .b(xor_4_out), .out(adder_4_out), .cin(adder_3_cout), .cout(adder_4_cout));
  // Probe on adder_3_out
  // Probe on adder_4_out
  Adder #(.width(1)) adder_5 (.a(in_6), .b(xor_5_out), .out(adder_5_out), .cin(adder_4_cout), .cout(adder_5_cout));
  // Probe on adder_5_out
  // Probe on adder_5_out
  // Probe on adder_6_out
  // Probe on nothing
  Adder #(.width(1)) adder_6 (.a(in_7), .b(xor_6_out), .out(adder_6_out), .cin(adder_5_cout), .cout(adder_6_cout));
  // Probe on adder_7_out
  // Probe on adder_8_out
  Adder #(.width(1)) adder_7 (.a(MSB), .b(xor_7_out), .out(adder_7_out), .cin(adder_6_cout), .cout(adder_7_cout));
  // Probe on adder_8_cout
  Adder #(.width(1)) adder_8 (.a(in_9), .b(xor_8_out), .out(adder_8_out), .cin(adder_7_cout), .cout(adder_8_cout));

  // Notes on the sheet:
  //   LSB
  //   LSB
  //   ->
  //   MSB
endmodule
