// Logisim project multiplier.circ as structural Verilog: 1 circuit, main circuit main
module main (
  input  [7:0] B,
  input  [7:0] A,
  input  in_3,
  input  in_4,
  input  in_5,
  input  [7:0] in_6,
  input  in_7,
  input  in_8,
  input  in_9,
  input  in_10,
  input  in_11,
  input  [7:0] in_12,
  output [7:0] out_13,
  output [7:0] out_14,
  output [7:0] out_15,
  output [7:0] out_16
);

  wire clock_1_out, comparator_1_eq, not_1_out;

  Clock clock_1 (.out(clock_1_out));
  Register register_1 (.D(in_6), .en(clock_1_out), .clk(clock_1_out), .Q(out_15), .clr(in_7));
  Register register_2 (.D(A), .en(clock_1_out), .clk(clock_1_out), .Q(out_13), .clr(in_3));
  not not_1 (not_1_out, comparator_1_eq);
  Counter counter_1 (
    .clr(in_8), .load(in_9), .up(in_10), .count(in_11), .clk(clock_1_out), .D(out_14), .Q(out_16));  // open: carry
  Register register_3 (.D(B), .en(clock_1_out), .clk(clock_1_out), .Q(out_14), .clr(in_5));
  Comparator comparator_1 (.a(out_16), .b(in_12), .eq(comparator_1_eq));  // open: gt, lt
  Adder adder_1 (.a(out_13), .b(out_15), .out(in_6), .cin(in_4));  // open: cout

  // Notes on the sheet:
  //   Result = Result + A 
endmodule
